// Logisim project CS1409_U201414797_张丹朱_cpu.circ as structural Verilog: 12 circuits, main circuit main
module main (
);

  wire alu_2_p4, alucount, ALUSrc, and_1_out, and_2_out, and_3_out, and_5_out, and_6_out, and_7_out,
       and_8_out, and_9_out, and_10_out, and_11_out, and_12_out, and_13_out, and_14_out, and_16_out, beq,
       bgtz, bne, BRANCH, branch_t, clk, clock_1_out, comparator_1_eq, D_syscall, demultiplexer_2_out1,
       demultiplexer_2_out2, demultiplexer_2_out3, demultiplexer_3_out1, demultiplexer_3_out2,
       demultiplexer_3_out3, E_j, E_jr, E_lw, E_mtc0, eret, ex_mem_1_m_jal, ex_mem_1_m_memtoreg,
       ex_mem_1_m_mfc0, ex_mem_1_m_regwrite, ex_mem_1_m_syscall, halt, hazard_unit_1_e_rs,
       hazard_unit_1_e_rt, hazard_unit_1_m_rs, hazard_unit_1_m_rt, highlow, I0, I1, I2, id_ex_1_e_alusrc,
       id_ex_1_e_beq, id_ex_1_e_bgtz, id_ex_1_e_bne, id_ex_1_e_ers, id_ex_1_e_ert, id_ex_1_e_jal,
       id_ex_1_e_memtoreg, id_ex_1_e_memwrite, id_ex_1_e_mfc0, id_ex_1_e_mrs, id_ex_1_e_mrt,
       id_ex_1_e_regwrite, id_ex_1_e_sel1, id_ex_1_e_sel2, id_ex_1_e_sh, id_ex_1_e_shift, id_ex_1_e_syscall,
       IE, IS, IS0, ISRC0_2_out, ISRC1_2_out, ISRC2_2_out, j, jal, jr, LOADUSE, lw, M_MenWrite, M_mtc0, M_sh,
       mem_wb_1_w_jal, mem_wb_1_w_mfc0, MentoReg, MenWrite, mfc0, mtc0, multiplexer_4_out, not_1_out,
       not_2_out, not_3_out, or_1_out, or_2_out, or_3_out, or_4_out, or_5_out, or_6_out, or_7_out, or_8_out,
       other, priority_encoder_1_en_out, priority_encoder_1_gs, readRs, readRt, RegDst, RegWrite, sel1, sel2,
       sh, shift, srav, syscall, W_mtc0, W_RegWrite;
  wire [1:0] CAUSE_q, priority_encoder_1_out;
  wire [3:0] ALUControl, id_ex_1_e_aluctr;
  wire [4:0] di_1_sa, E_rd, ex_mem_1_m_rw, id_ex_1_e_rw, M_rd, multiplexer_6_out, multiplexer_7_out, rd, rs,
       rt, W_rd, W_RW;
  wire [5:0] funct, op;
  wire [9:0] demultiplexer_1_out0, demultiplexer_1_out1, register_3_q_2;
  wire [11:0] adder_1_out, adder_3_out, counter_1_q, counter_2_q, counter_3_q, counter_4_q, counter_5_q,
       counter_6_q, counter_7_q, counter_8_q, finish;
  wire [15:0] di_1_imm_16bit, ram_1_data;
  wire [25:0] di_1_imm_26bit;
  wire [27:0] bit_extender_3_out, shifter_1_out;
  wire [31:0] a0, adder_2_out, adder_4_out, alu_2_p5, bit_extender_2_out, bit_extender_4_out,
       bit_extender_5_out, cp0data, D_cp0data, E_cp0data, epc, ex_mem_1_m_pc_4, ex_mem_1_m_r, id_ex_1_e_imm,
       id_ex_1_e_offset, id_ex_1_e_pc_4, id_ex_1_e_r1, id_ex_1_e_r2, id_ex_1_e_shamt, if_id_1_d_i,
       if_id_1_d_pc_4, M_cp0data, main_1_reg1, main_1_reg2_2, mem_wb_1_w_d, mem_wb_1_w_pc_4,
       multiplexer_1_out, multiplexer_2_out, multiplexer_3_out, multiplexer_5_out, multiplexer_8_out,
       multiplexer_9_out, multiplexer_10_out, multiplexer_11_out, multiplexer_12_out, multiplexer_13_out,
       multiplexer_14_out, multiplexer_15_out, multiplexer_16_out, multiplexer_18_out, multiplexer_19_out,
       multiplexer_20_out, multiplexer_21_out, multiplexer_22_out, multiplexer_23_out, multiplexer_24_out,
       multiplexer_25_out, multiplexer_26_out, pcbuf, register_1_q, register_2_q, register_3_q, register_5_q,
       rf2, rom_1_data, rom_2_data, shifter_2_out, v0, W_cp0data;
  wire [31:1] STATUS_q;
  wire [31:2] CAUSE_q_2;
  wire [31:16] ram_1_data_2;

  // Probe on multiplexer_1_out
  Multiplexer #(.width(32), .enable("false")) multiplexer_1 (
    .in0(multiplexer_21_out), .in1(id_ex_1_e_r1), .out(multiplexer_1_out), .sel(E_jr));
  not not_1 (not_1_out, halt);
  or or_1 (or_1_out, MenWrite, MentoReg);
  Counter #(.width(12), .max('hfff)) counter_1 (
    .load(1'b0), .D({12{1'b0}}), .count(other), .Q(counter_1_q), .clk(clk), .clr(1'b0));  // open: carry
  Register #(.width(32)) register_1 (
    .D({register_3_q[31:12], register_3_q_2, register_3_q[1:0]}), .en(1'b1), .Q(register_1_q), .clk(clk));  // open: clr
  Multiplexer #(.width(32), .enable("false")) multiplexer_2 (
    .in0(multiplexer_1_out), .in1(epc), .out(multiplexer_2_out), .sel(eret));
  assign finish = {{11{1'b0}}, not_1_out};  // Bit_Extender bit_extender_1
  // Probe on counter_2_q
  Counter #(.width(12), .max('hfff)) counter_2 (
    .load(1'b0), .D({12{1'b0}}), .count(alucount), .Q(counter_2_q), .clk(clk), .clr(1'b0));  // open: carry
  Counter #(.width(12), .max('hfff)) counter_3 (
    .load(1'b0), .D({12{1'b0}}), .count(or_1_out), .Q(counter_3_q), .clk(clk), .clr(1'b0));  // open: carry
  // Probe on counter_3_q
  Register #(.width(32)) register_2 (.D(register_1_q), .en(1'b1), .Q(register_2_q), .clk(clk));  // open: clr
  // Probe on multiplexer_3_out
  Multiplexer #(.width(32), .enable("false")) multiplexer_3 (
    .in0(multiplexer_2_out), .in1(32'h80000000), .out(multiplexer_3_out), .sel(IS));
  and and_1 (and_1_out, halt, ~LOADUSE);  // AND_Gate
  // Probe on v0
  Comparator #(.width(32)) comparator_1 (.a(v0), .b(32'ha), .eq(comparator_1_eq));  // open: gt, lt
  // Probe on adder_1_out
  Adder #(.width(12)) adder_1 (.a(counter_1_q), .b(finish), .out(adder_1_out), .cin(1'b0));  // open: cout
  // Probe on {register_3_q[31:12], register_3_q_2, register_3_q[1:0]}
  Register #(.width(32)) register_3 (
    .D(multiplexer_3_out), .en(and_1_out), .Q({register_3_q[31:12], register_3_q_2, register_3_q[1:0]}),
    .clk(multiplexer_4_out), .clr(1'b0));
  Multiplexer #(.enable("false")) multiplexer_4 (.in0(clk), .in1(not_2_out), .out(multiplexer_4_out), .sel(IS));
  not not_2 (not_2_out, clk);
  not not_3 (not_3_out, comparator_1_eq);
  and and_2 (and_2_out, comparator_1_eq, syscall);
  not not_4 (halt, and_2_out);
  Register #(.width(32)) register_4 (.D(register_2_q), .en(1'b1), .Q(pcbuf), .clk(IS0));  // open: clr
  Demultiplexer #(.width(10), .enable("false")) demultiplexer_1 (
    .out0(demultiplexer_1_out0), .out1(demultiplexer_1_out1), .in(register_3_q_2), .sel(register_3_q[31]));
  Adder #(.width(32)) adder_2 (
    .a({register_3_q[31:12], register_3_q_2, register_3_q[1:0]}), .b(32'h4), .out(adder_2_out));  // open: cin, cout
  and and_3 (and_3_out, syscall, not_3_out);
  Counter #(.width(12), .max('hfff)) counter_4 (
    .D({12{1'b0}}), .count(1'b1), .Q(counter_4_q), .clk(clk), .clr(1'b0));  // open: load, carry
  Counter #(.width(12), .max('hfff)) counter_5 (
    .load(1'b0), .D({12{1'b0}}), .count(or_2_out), .Q(counter_5_q), .clk(clk), .clr(1'b0));  // open: carry
  or or_2 (or_2_out, j, jr);
  Counter #(.width(12), .max('hfff)) counter_6 (
    .load(1'b0), .D({12{1'b0}}), .count(or_3_out), .Q(counter_6_q), .clk(clk), .clr(1'b0));  // open: carry
  or or_3 (or_3_out, beq, bne);
  and and_4 (clk, clock_1_out, halt);
  Clock clock_1 (.out(clock_1_out));
  // Probe on adder_2_out
  // Probe on a0
  Register #(.width(32)) register_5 (.D(a0), .en(and_3_out), .Q(register_5_q), .clk(clk), .clr(1'b0));
  Adder #(.width(12)) adder_3 (.a(counter_4_q), .b(finish), .out(adder_3_out), .cin(1'b0));  // open: cout
  // Probe on adder_3_out
  // Probe on counter_5_q
  // Probe on counter_6_q
  ROM #(.addrWidth(10), .dataWidth(32)) rom_1 (.addr(demultiplexer_1_out0), .data(rom_1_data), .sel(1'b1));
  ROM #(.addrWidth(10), .dataWidth(32)) rom_2 (.addr(demultiplexer_1_out1), .data(rom_2_data), .sel(1'b1));
  Hex_Digit_Display hex_digit_display_1 (.value(register_5_q[27:24]));  // open: dp
  Hex_Digit_Display hex_digit_display_2 (.value(register_5_q[31:28]));  // open: dp
  Multiplexer #(.width(32)) multiplexer_5 (
    .in0(rom_1_data), .in1(rom_2_data), .out(multiplexer_5_out), .sel(register_3_q[31]), .en(1'b1));
  Hex_Digit_Display hex_digit_display_3 (.value(register_5_q[19:16]));  // open: dp
  Hex_Digit_Display hex_digit_display_4 (.value(register_5_q[23:20]));  // open: dp
  Counter #(.width(12), .max('hfff)) counter_7 (
    .load(1'b0), .D({12{1'b0}}), .count(BRANCH), .Q(counter_7_q), .clk(clk), .clr(1'b0));  // open: carry
  // Probe on counter_7_q
  IF_ID if_id_1 (
    .F_I(multiplexer_5_out), .clk(clk), .D_I(if_id_1_d_i), .F_PC_4(adder_2_out), .D_PC_4(if_id_1_d_pc_4),
    .clr(or_4_out), .EN(LOADUSE), .F_cp0data(cp0data), .D_cp0data(D_cp0data));
  Hex_Digit_Display hex_digit_display_5 (.value(register_5_q[11:8]));  // open: dp
  Hex_Digit_Display hex_digit_display_6 (.value(register_5_q[15:12]));  // open: dp
  // Probe on if_id_1_d_i
  Hex_Digit_Display hex_digit_display_7 (.value(register_5_q[3:0]));  // open: dp
  Hex_Digit_Display hex_digit_display_8 (.value(register_5_q[7:4]));  // open: dp
  Counter #(.width(12), .max('hfff)) counter_8 (
    .load(1'b0), .D({12{1'b0}}), .count(LOADUSE), .Q(counter_8_q), .clk(clk), .clr(1'b0));  // open: carry
  // Probe on ALUControl
  ControlUnit ControlUnit (
    .Op(op), .Funct(funct), .MentoReg(MentoReg), .MemWrite(MenWrite), .ALUControl(ALUControl),
    .ALUSrc(ALUSrc), .RegDst(RegDst), .RegWrite(RegWrite), .jr(jr), .j(j), .shift(shift), .beq(beq),
    .bne(bne), .syscall(D_syscall), .jal(jal), .alucount(alucount), .other_count(other), .srav(srav),
    .sh(sh), .bgtz(bgtz), .Rs(rs), .eret(eret), .mfc0(mfc0), .mtc0(mtc0), .sel2(sel2), .sel1(sel1),
    .readRs(readRs), .readRt(readRt), .lw(lw));
  // Probe on if_id_1_d_pc_4
  or or_4 (or_4_out, IS0, BRANCH);
  // Probe on counter_8_q
  DI di_1 (
    .IR(if_id_1_d_i), .imm_26bit(di_1_imm_26bit), .imm_16bit(di_1_imm_16bit), .funct(funct), .sa(di_1_sa),
    .rd(rd), .rt(rt), .rs(rs), .op(op));
  Hazard_Unit hazard_unit_1 (
    .Rs(rs), .Rt(rt), .E_RW(id_ex_1_e_rw), .M_RW(ex_mem_1_m_rw), .E_Rs(hazard_unit_1_e_rs),
    .M_Rs(hazard_unit_1_m_rs), .E_Rt(hazard_unit_1_e_rt), .M_Rt(hazard_unit_1_m_rt),
    .E_RegWrite(id_ex_1_e_regwrite), .M_RegWrite(ex_mem_1_m_regwrite), .readRs(readRs), .readRt(readRt),
    .branch(branch_t), .E_jr(E_jr), .BRANCH_2(BRANCH), .E_LW(E_lw), .LOADUSE(LOADUSE), .E_j(E_j), .clk(clk));
  LED ISRC0 (.in(I0));
  // Probe on v0
  Multiplexer #(.width(5), .enable("false")) multiplexer_6 (.in0(rt), .in1(rd), .out(multiplexer_6_out), .sel(RegDst));
  assign bit_extender_2_out = {{27{1'b0}}, di_1_sa};  // Bit_Extender bit_extender_2
  assign bit_extender_3_out = {{2{di_1_imm_26bit[25]}}, di_1_imm_26bit};  // Bit_Extender bit_extender_3
  LED ISRC1 (.in(I1));
  // Probe on multiplexer_7_out
  Multiplexer #(.width(5), .enable("false")) multiplexer_7 (
    .in0(multiplexer_6_out), .in1({5{1'b1}}), .out(multiplexer_7_out), .sel(jal));
  // Probe on multiplexer_25_out
  // Probe on bit_extender_2_out
  assign bit_extender_4_out = {{16{di_1_imm_16bit[15]}}, di_1_imm_16bit};  // Bit_Extender bit_extender_4
  Shifter #(.width(28)) shifter_1 (.in(bit_extender_3_out), .\dist (5'b00010), .out(shifter_1_out));
  LED ISRC2 (.in(I2));
  // Probe on a0
  // Probe on bit_extender_4_out
  // Probe on {if_id_1_d_pc_4[31:28], shifter_1_out}
  // Probe on shifter_1_out
  \CS1409_U201414797_张丹朱_regfile_main  main_1 (
    .Reg1_num(rs), .Reg2(rt), .Write_Reg_num(W_RW), .Din(multiplexer_25_out), .Write_Enable(W_RegWrite),
    .Clock(clk), .Reg1(main_1_reg1), .Reg2_2(main_1_reg2_2), .v0(v0), .a0(a0));  // open: s0_Value, s1_Value, s2_Value, ra_Value
  // Probe on main_1_reg2_2
  Demultiplexer #(.select(2), .enable("false")) demultiplexer_2 (
    .out1(demultiplexer_2_out1), .out2(demultiplexer_2_out2), .out3(demultiplexer_2_out3), .in(1'b1),
    .sel(W_rd[1:0]));  // open: out0
  // Probe on multiplexer_7_out
  ID_EX id_ex_1 (
    .E_MemtoReg(id_ex_1_e_memtoreg), .D_MemtoReg(MentoReg), .E_MemWrite(id_ex_1_e_memwrite),
    .D_MemWrite(MenWrite), .clk(clk), .E_beq(id_ex_1_e_beq), .D_beq(beq), .E_bne(id_ex_1_e_bne), .D_bne(bne),
    .E_bgtz(id_ex_1_e_bgtz), .D_bgtz(bgtz), .E_sh(id_ex_1_e_sh), .D_sh(sh), .E_R1(id_ex_1_e_r1),
    .D_R1(main_1_reg1), .E_R2(id_ex_1_e_r2), .D_R2(main_1_reg2_2), .E_imm(id_ex_1_e_imm),
    .D_imm(bit_extender_4_out), .E_pc_4(id_ex_1_e_pc_4), .D_pc_4(if_id_1_d_pc_4),
    .E_offset(id_ex_1_e_offset), .D_offset({if_id_1_d_pc_4[31:28], shifter_1_out}),
    .E_ALUCTR(id_ex_1_e_aluctr), .D_ALUCTR(ALUControl), .E_shamt(id_ex_1_e_shamt),
    .D_shamt(bit_extender_2_out), .E_j(E_j), .D_j(j), .D_RW(multiplexer_7_out), .E_RW(id_ex_1_e_rw),
    .E_RegWrite(id_ex_1_e_regwrite), .D_RegWrite(RegWrite), .E_syscall(id_ex_1_e_syscall),
    .D_syscall(D_syscall), .E_jal(id_ex_1_e_jal), .D_jal(jal), .E_shift(id_ex_1_e_shift), .D_shift(shift),
    .E_ALUSrc(id_ex_1_e_alusrc), .D_ALUSrc(ALUSrc), .E_mfc0(id_ex_1_e_mfc0), .D_mfc0(mfc0),
    .E_sel1(id_ex_1_e_sel1), .D_sel1(sel1), .E_sel2(id_ex_1_e_sel2), .D_sel2(sel2),
    .D_ERs(hazard_unit_1_e_rs), .E_MRs(id_ex_1_e_mrs), .D_MRs(hazard_unit_1_m_rs), .E_ERt(id_ex_1_e_ert),
    .D_ERt(hazard_unit_1_e_rt), .E_MRt(id_ex_1_e_mrt), .D_MRt(hazard_unit_1_m_rt), .E_ERs(id_ex_1_e_ers),
    .E_jr(E_jr), .D_jr(jr), .E_lw(E_lw), .D_lw(lw), .clr(or_5_out), .D_rd(rd), .E_rd(E_rd), .D_mtc0(mtc0),
    .E_mtc0(E_mtc0), .D_cp0data(D_cp0data), .E_cp0data(E_cp0data));
  // Probe on main_1_reg1
  or or_5 (or_5_out, or_4_out, LOADUSE);
  and and_5 (and_5_out, demultiplexer_2_out1, W_mtc0);
  and and_6 (and_6_out, demultiplexer_2_out2, W_mtc0);
  and and_7 (and_7_out, demultiplexer_2_out3, W_mtc0);
  Button ISRC0_2 (.out(ISRC0_2_out));
  Button ISRC1_2 (.out(ISRC1_2_out));
  Button ISRC2_2 (.out(ISRC2_2_out));
  // Probe on id_ex_1_e_r2
  Multiplexer #(.width(32), .enable("false")) multiplexer_8 (
    .in0(id_ex_1_e_r2), .in1(mem_wb_1_w_d), .out(multiplexer_8_out), .sel(id_ex_1_e_mrt));
  Multiplexer #(.width(32), .enable("false")) multiplexer_9 (
    .in0(bit_extender_5_out), .in1(rf2), .out(multiplexer_9_out), .sel(and_7_out));
  // Probe on id_ex_1_e_rw
  // Probe on id_ex_1_e_r1
  Multiplexer #(.width(32), .enable("false")) multiplexer_10 (
    .in0(multiplexer_8_out), .in1({ex_mem_1_m_r[31:2], highlow, ex_mem_1_m_r[0]}), .out(multiplexer_10_out),
    .sel(id_ex_1_e_ert));
  Multiplexer #(.width(32), .enable("false")) multiplexer_11 (
    .in0(rf2), .in1(pcbuf), .out(multiplexer_11_out), .sel(IS0));
  or or_6 (or_6_out, and_5_out, IS0);
  or or_7 (or_7_out, IS0, and_7_out);
  Register #(.width(1)) IR0 (.D(1'b1), .en(1'b1), .Q(I0), .clk(ISRC0_2_out), .clr(demultiplexer_3_out1));
  Register #(.width(1)) IR1 (.D(1'b1), .en(1'b1), .Q(I1), .clk(ISRC1_2_out), .clr(demultiplexer_3_out2));
  Register #(.width(1)) IR2 (.D(1'b1), .en(1'b1), .Q(I2), .clk(ISRC2_2_out), .clr(demultiplexer_3_out3));
  Demultiplexer #(.select(2), .enable("false")) demultiplexer_3 (
    .out1(demultiplexer_3_out1), .out2(demultiplexer_3_out2), .out3(demultiplexer_3_out3), .in(and_16_out),
    .sel(CAUSE_q));  // open: out0
  // Probe on multiplexer_10_out
  Multiplexer #(.width(32), .enable("false")) multiplexer_12 (
    .in0(id_ex_1_e_r1), .in1(mem_wb_1_w_d), .out(multiplexer_12_out), .sel(id_ex_1_e_mrs));
  Multiplexer #(.width(32), .enable("false")) multiplexer_13 (
    .in0(multiplexer_12_out), .in1({ex_mem_1_m_r[31:2], highlow, ex_mem_1_m_r[0]}), .out(multiplexer_13_out),
    .sel(id_ex_1_e_ers));
  // Probe on id_ex_1_e_pc_4
  Register #(.width(32)) u_EPC (.D(multiplexer_11_out), .en(or_6_out), .Q(epc), .clk(clk), .clr(1'b0));
  Register #(.width(32)) STATUS (.D(rf2), .en(and_6_out), .Q({STATUS_q, IE}), .clk(clk), .clr(1'b0));
  Register #(.width(32)) CAUSE (.D(multiplexer_9_out), .en(or_7_out), .Q({CAUSE_q_2, CAUSE_q}), .clk(clk), .clr(1'b0));
  Multiplexer #(.width(32), .enable("false")) multiplexer_14 (
    .in0(multiplexer_10_out), .in1(id_ex_1_e_imm), .out(multiplexer_14_out), .sel(id_ex_1_e_alusrc));
  // Probe on id_ex_1_e_shamt
  // Probe on id_ex_1_e_imm
  // Probe on multiplexer_13_out
  Multiplexer #(.width(32), .enable("false")) multiplexer_15 (
    .in0(multiplexer_13_out), .in1(multiplexer_10_out), .out(multiplexer_15_out), .sel(id_ex_1_e_sel1));
  Multiplexer #(.width(32), .enable("false")) multiplexer_16 (
    .in0(multiplexer_14_out), .in1(id_ex_1_e_shamt), .out(multiplexer_16_out), .sel(id_ex_1_e_shift));
  // Probe on id_ex_1_e_offset
  // Probe on multiplexer_21_out
  Multiplexer #(.select(2), .width(32), .enable("false")) multiplexer_17 (
    .in0({32{1'b0}}), .in1(epc), .in2({STATUS_q, IE}), .in3({CAUSE_q_2, CAUSE_q}), .out(cp0data),
    .sel(W_rd[1:0]));
  or or_8 (or_8_out, CAUSE_q[0], CAUSE_q[1]);
  and and_8 (and_8_out, CAUSE_q[0], CAUSE_q[1]);
  // Probe on multiplexer_18_out
  Multiplexer #(.width(32), .enable("false")) multiplexer_18 (
    .in0(multiplexer_15_out), .in1({32{1'b0}}), .out(multiplexer_18_out), .sel(id_ex_1_e_bgtz));
  // Probe on multiplexer_19_out
  Multiplexer #(.width(32), .enable("false")) multiplexer_19 (
    .in0(multiplexer_16_out), .in1(multiplexer_13_out), .out(multiplexer_19_out), .sel(id_ex_1_e_sel2));
  // Probe on id_ex_1_e_aluctr
  Shifter #(.width(32)) shifter_2 (.in(id_ex_1_e_imm), .\dist (5'b00010), .out(shifter_2_out));
  and and_9 (and_9_out, I0, ~or_8_out);  // AND_Gate
  and and_10 (and_10_out, I1, ~CAUSE_q[1]);  // AND_Gate
  and and_11 (and_11_out, I2, ~and_8_out);  // AND_Gate
  // ALU alu_2: pin names not known; wires that end beside it: multiplexer_18_out, multiplexer_19_out, id_ex_1_e_aluctr, alu_2_p4, alu_2_p5
  and and_12 (and_12_out, id_ex_1_e_beq, alu_2_p4);
  and and_13 (and_13_out, ~alu_2_p4, id_ex_1_e_bne);  // AND_Gate
  or or_9 (branch_t, and_12_out, and_13_out, and_14_out);
  Adder #(.width(32)) adder_4 (.a(shifter_2_out), .b(id_ex_1_e_pc_4), .out(adder_4_out));  // open: cin, cout
  assign bit_extender_5_out = {{30{1'b0}}, priority_encoder_1_out};  // Bit_Extender bit_extender_5
  Priority_Encoder #(.select(2)) priority_encoder_1 (
    .in0(1'b0), .in1(and_9_out), .in2(and_10_out), .in3(and_11_out), .out(priority_encoder_1_out),
    .gs(priority_encoder_1_gs), .en_out(priority_encoder_1_en_out), .en_in(1'b1));
  // Probe on alu_2_p5
  and and_14 (and_14_out, alu_2_p5[0], id_ex_1_e_bgtz);
  Multiplexer #(.width(32), .enable("false")) multiplexer_20 (
    .in0(adder_2_out), .in1(adder_4_out), .out(multiplexer_20_out), .sel(branch_t));
  Multiplexer #(.width(32), .enable("false")) multiplexer_21 (
    .in0(multiplexer_20_out), .in1(id_ex_1_e_offset), .out(multiplexer_21_out), .sel(E_j));
  and and_15 (IS0, priority_encoder_1_gs, ~IE, ~eret);  // AND_Gate
  EX_MEM ex_mem_1 (
    .clk(clk), .M_jal(ex_mem_1_m_jal), .E_jal(id_ex_1_e_jal), .M_MemtoReg(ex_mem_1_m_memtoreg),
    .E_MemtoReg(id_ex_1_e_memtoreg), .M_MemWrite(M_MenWrite), .E_MemWrite(id_ex_1_e_memwrite), .M_sh(M_sh),
    .E_sh(id_ex_1_e_sh), .E_R2(multiplexer_10_out), .M_R2(rf2), .E_pc_4(id_ex_1_e_pc_4),
    .M_pc_4(ex_mem_1_m_pc_4), .E_R(alu_2_p5), .M_R({ex_mem_1_m_r[31:2], highlow, ex_mem_1_m_r[0]}),
    .E_RW(id_ex_1_e_rw), .M_RW(ex_mem_1_m_rw), .M_RegWrite(ex_mem_1_m_regwrite),
    .E_RegWrite(id_ex_1_e_regwrite), .M_syscall(ex_mem_1_m_syscall), .E_syscall(id_ex_1_e_syscall),
    .M_mfc0(ex_mem_1_m_mfc0), .E_mfc0(id_ex_1_e_mfc0), .E_rd(E_rd), .M_rd(M_rd), .E_mtc0(E_mtc0),
    .M_mtc0(M_mtc0), .E_cp0data(E_cp0data), .M_cp0data(M_cp0data));
  // Probe on {ex_mem_1_m_r[31:2], highlow, ex_mem_1_m_r[0]}
  D_Flip_Flop d_ff_1 (.clk(clk), .D(IS0), .Q(IS), .preset(1'b0), .en(1'b1), .reset(and_16_out));  // open: Qn
  and and_16 (and_16_out, ~clk, IS);  // AND_Gate
  // Probe on rf2
  // Probe on ex_mem_1_m_pc_4
  Multiplexer #(.width(32), .enable("false")) multiplexer_22 (
    .in0({ram_1_data_2, rf2[15:0]}), .in1({rf2[15:0], ram_1_data}), .out(multiplexer_22_out), .sel(highlow));
  // Probe on ex_mem_1_m_rw
  Multiplexer #(.width(32), .enable("false")) multiplexer_23 (
    .in0(rf2), .in1(multiplexer_22_out), .out(multiplexer_23_out), .sel(M_sh));
  // Probe on multiplexer_23_out
  RAM #(.addrWidth(24), .dataWidth(32), .bus("separate")) ram_1 (
    .addr(ex_mem_1_m_r[25:2]), .din(multiplexer_23_out), .data({ram_1_data_2, ram_1_data}), .str(M_MenWrite),
    .sel(1'b1), .clk(clk), .ld(1'b1), .clr(1'b0));
  // Probe on {ram_1_data_2, ram_1_data}
  MEM_WB mem_wb_1 (
    .clk(clk), .M_MemtoReg(ex_mem_1_m_memtoreg), .M_D(multiplexer_24_out), .W_D(mem_wb_1_w_d),
    .M_RW(ex_mem_1_m_rw), .W_RW(W_RW), .W_syscall(syscall), .M_syscall(ex_mem_1_m_syscall),
    .W_RegWrite(W_RegWrite), .M_RegWrite(ex_mem_1_m_regwrite), .W_mfc0(mem_wb_1_w_mfc0),
    .M_mfc0(ex_mem_1_m_mfc0), .W_jal(mem_wb_1_w_jal), .M_jal(ex_mem_1_m_jal), .M_PC_4(ex_mem_1_m_pc_4),
    .W_PC_4(mem_wb_1_w_pc_4), .M_rd(M_rd), .W_rd(W_rd), .M_mtc0(M_mtc0), .W_mtc0(W_mtc0),
    .M_cp0data(M_cp0data), .W_cp0data(W_cp0data));  // open: W_MemtoReg, M_R, W_R
  Multiplexer #(.width(32), .enable("false")) multiplexer_24 (
    .in0({ex_mem_1_m_r[31:2], highlow, ex_mem_1_m_r[0]}), .in1({ram_1_data_2, ram_1_data}),
    .out(multiplexer_24_out), .sel(ex_mem_1_m_memtoreg));
  // Probe on multiplexer_24_out
  // Probe on mem_wb_1_w_d
  // Probe on multiplexer_25_out
  // Probe on mem_wb_1_w_pc_4
  // Probe on W_RW
  Multiplexer #(.width(32), .enable("false")) multiplexer_25 (
    .in0(multiplexer_26_out), .in1(cp0data), .out(multiplexer_25_out), .sel(mem_wb_1_w_mfc0));
  Multiplexer #(.width(32), .enable("false")) multiplexer_26 (
    .in0(mem_wb_1_w_d), .in1(mem_wb_1_w_pc_4), .out(multiplexer_26_out), .sel(mem_wb_1_w_jal));

  // Notes on the sheet:
  //   IF  取指令   ID 指令译码   EX 执行运算  MEM 访存阶段  WB 结果写回
  //   contents of rom_1 (hex, n*v repeats v):
  //   20110001 8000c05 20110001 20120002 20130003 8000c09 20110001 20120002 20130003 8000c0d 20110001
  //   20120002 20130003 8000c11 20110001 20120002 20130003 c000cb8 20100001 20110001 118fc0 112020
  //   20020022 c 118882 12200001 8000c15 112020 20020022 c 20110001 118880 112020 20020022 c 12200001
  //   8000c1f 20110001 118fc0 112020 20020022 c 1188c3 112020 20020022 c 118903 112020 20020022 c 118903
  //   112020 20020022 c 118903 112020 20020022 c 118903 112020 20020022 c 118903 112020 20020022 c 118903
  //   112020 20020022 c 118903 112020 20020022 c 20100001 109fc0 139fc3 8021 2012000c 24160003 26100001
  //   3210000f 20080008 20090001 139900 2709825 132020 20020022 c 1094022 1500fff9 22100001 2018000f
  //   2188024 108700 20080008 20090001 139902 2709825 132021 20020022 c 1094022 1500fff9 108702 2c9b022
  //   12c00001 8000c50 4020 1084027 84400 3508ffff 82021 20020022 c 2010ffff 20110000 ae300000 22100001
  //   22310004 ae300000 22100001 22310004 ae300000 22100001 22310004 ae300000 22100001 22310004 ae300000
  //   22100001 22310004 ae300000 22100001 22310004 ae300000 22100001 22310004 ae300000 22100001 22310004
  //   ae300000 22100001 22310004 ae300000 22100001 22310004 ae300000 22100001 22310004 ae300000 22100001
  //   22310004 ae300000 22100001 22310004 ae300000 22100001 22310004 ae300000 22100001 22310004 ae300000
  //   22100001 22310004 22100001 8020 2011003c 8e130000 8e340000 274402a 11000002 ae330000 ae140000
  //   2231fffc 1611fff8 102020 20020022 c 22100004 2011003c 1611fff2 2002000a c 20100000 22100001 102020
  //   20020022 c 22100002 102020 20020022 c 22100003 102020 20020022 c 22100004 102020 20020022 c 22100005
  //   102020 20020022 c 22100006 102020 20020022 c 22100007 102020 20020022 c 22100008 102020 20020022
  //   20020022 c 3e00008
  //   contents of rom_2 (hex, n*v repeats v):
  //   201a0001 409a1000 201c0800 39df020 401a0800 afda0000 23defffc 23bdfffc afc40000 23bdfffc 23defffc
  //   afc20000 23bdfffc 23defffc afc80000 23bdfffc 23defffc afc90000 23bdfffc 23defffc afca0000 23bdfffc
  //   23defffc 2009ffe8 13a90004 afc80000 23defffc 23bdfffc 15200004 20090000 afc90000 23defffc 23bdfffc
  //   201a0000 409a1000 40081800 20020003 11020008 20090008 82020 200a0001 c 42100 12a4822 1520fffc
  //   11200010 20044000 20090001 200a0804 c 214a0002 1242007 a5440001 1c80fffb 20040aaa 20090555 892026 c
  //   20040aaa 20090aaa 892026 c 201a0001 409a1000 23de0004 23bd0004 8fda0000 409a1800 23de0004 23bd0004
  //   8fca0000 23de0004 23bd0004 8fc90000 23de0004 23bd0004 8fc80000 23de0004 23bd0004 8fc20000 23de0004
  //   23bd0004 8fc40000 23de0004 23bd0004 8fda0000 409a0800 201a0000 409a1000 42000018
endmodule

module ControlUnit (
  input  [4:0] Rs,
  input  [5:0] Op,
  input  [5:0] Funct,
  output alucount,
  output readRs,
  output readRt,
  output other_count,
  output mtc0,
  output mfc0,
  output eret,
  output srav,
  output sh,
  output bgtz,
  output syscall,
  output jal,
  output bne,
  output beq,
  output jr,
  output MentoReg,
  output lw,
  output sel2,
  output j,
  output MemWrite,
  output shift,
  output RegDst,
  output RegWrite,
  output ALUSrc,
  output sel1,
  output [3:0] ALUControl
);

  wire ADD_out, AND_out, OR_16_out, SLT_out, SUB_out, type1_1_add, type1_1_addi, type1_1_addiu, type1_1_addu,
       type1_1_and, type1_1_andi, type1_1_or, type1_1_ori, type1_1_sll, type1_1_sra, type1_1_srl,
       type1_1_sub, type2_1_j, type2_1_nor, type2_1_slt, type2_1_slti, type2_1_sltu, type2_1_sw, type3_1_xor;

  type0 type0_1 (
    .op0(Op[0]), .op1(Op[1]), .op2(Op[2]), .op3(Op[3]), .op4(Op[4]), .op5(Op[5]), .rs0(Rs[0]), .rs1(Rs[1]),
    .rs2(Rs[2]), .rs3(Rs[3]), .rs4(Rs[4]), .mfc0(mfc0), .mtc0(mtc0));
  type3 type3_1 (
    .op0(Op[0]), .op1(Op[1]), .op2(Op[2]), .op3(Op[3]), .op4(Op[4]), .op5(Op[5]), .funct0(Funct[0]),
    .funct1(Funct[1]), .funct2(Funct[2]), .funct3(Funct[3]), .funct4(Funct[4]), .funct5(Funct[5]),
    .srav(srav), .\xor (type3_1_xor), .sh(sh), .bgtz(bgtz), .eret(eret));
  type1 type1_1 (
    .op0(Op[0]), .op1(Op[1]), .op2(Op[2]), .op3(Op[3]), .op4(Op[4]), .op5(Op[5]), .funct0(Funct[0]),
    .funct1(Funct[1]), .funct2(Funct[2]), .funct3(Funct[3]), .funct4(Funct[4]), .funct5(Funct[5]),
    .add(type1_1_add), .addi(type1_1_addi), .addiu(type1_1_addiu), .addu(type1_1_addu), .\and (type1_1_and),
    .andi(type1_1_andi), .sll(type1_1_sll), .sra(type1_1_sra), .srl(type1_1_srl), .sub(type1_1_sub),
    .\or (type1_1_or), .ori(type1_1_ori));
  type2 type2_1 (
    .op0(Op[0]), .op1(Op[1]), .op2(Op[2]), .op3(Op[3]), .op4(Op[4]), .op5(Op[5]), .funct0(Funct[0]),
    .funct1(Funct[1]), .funct2(Funct[2]), .funct3(Funct[3]), .funct4(Funct[4]), .funct5(Funct[5]),
    .\nor (type2_1_nor), .lw(lw), .sw(type2_1_sw), .beq(beq), .bne(bne), .slt(type2_1_slt),
    .slti(type2_1_slti), .sltu(type2_1_sltu), .j(type2_1_j), .jal(jal), .jr(jr), .syscall(syscall));
  or or_1 (readRs, type1_1_add, type1_1_addi, type1_1_addiu, type1_1_addu, type1_1_and, type1_1_andi, type1_1_sub, type1_1_or, type1_1_ori, type2_1_nor, lw, type2_1_sw, beq, bne, type2_1_slt, type2_1_slti, type2_1_sltu, jr);
  or or_2 (readRt, type1_1_add, type1_1_addu, type1_1_and, type1_1_sll, type1_1_sra, type1_1_srl, type1_1_sub, type1_1_or, type2_1_nor, type2_1_sw, beq, bne, type2_1_slt, type2_1_sltu, mfc0, mtc0);
  or or_3 (sel2, bgtz, srav);
  or or_4 (sel1, srav, shift);
  or or_5 (other_count, syscall, type2_1_sltu, type2_1_slti, type2_1_slt, type1_1_addu);
  or or_6 (alucount, type1_1_add, type1_1_addi, type1_1_addiu, type1_1_and, type1_1_andi, type1_1_sll, type1_1_sra, type1_1_srl, type1_1_sub, type1_1_or, type1_1_ori, type2_1_nor);
  or or_7 (j, jal, type2_1_j);
  or or_8 (MemWrite, type2_1_sw, sh);
  or or_9 (shift, type1_1_srl, type1_1_sra, type1_1_sll);
  or or_10 (RegDst, srav, type2_1_sltu, type2_1_slt, type2_1_nor, type1_1_or, type1_1_sub, type1_1_srl, type1_1_sra, type1_1_sll, type1_1_and, type1_1_addu, type1_1_add, type3_1_xor);
  or or_11 (RegWrite, srav, jal, type2_1_sltu, type2_1_slti, type2_1_slt, lw, type2_1_nor, type1_1_ori, type1_1_or, type1_1_sub, mfc0, type1_1_srl, type1_1_sra, type1_1_sll, type1_1_andi, type1_1_and, type1_1_addu, type1_1_addiu, type1_1_addi, type1_1_add, type3_1_xor);
  or or_12 (ALUSrc, sh, type2_1_slti, type2_1_sw, lw, type1_1_ori, type1_1_andi, type1_1_addiu, type1_1_addi);
  or ADD (ADD_out, type2_1_sw, lw, type1_1_addu, type1_1_addiu, type1_1_addi, type1_1_add);
  or SUB (SUB_out, bne, beq, type1_1_sub);
  or or_13 (ALUControl[3], type3_1_xor, type2_1_sltu, type2_1_nor, OR_16_out, SLT_out, bgtz);
  or AND (AND_out, type1_1_andi, type1_1_and);
  or or_14 (ALUControl[1], AND_out, type1_1_srl, type2_1_nor, SUB_out, SLT_out, bgtz);
  or or_15 (ALUControl[2], type2_1_sltu, ADD_out, sh, SUB_out, AND_out);
  or OR_16 (OR_16_out, type1_1_ori, type1_1_or);
  or or_17 (ALUControl[0], bgtz, type3_1_xor, type1_1_sra, ADD_out, AND_out, SLT_out, srav, sh);
  or SLT (SLT_out, type2_1_slti, type2_1_slt);

  assign MentoReg = lw;
endmodule

module DI (
  input  [31:0] IR,
  output [25:0] imm_26bit,
  output [15:0] imm_16bit,
  output [5:0] funct,
  output [4:0] sa,
  output [4:0] rd,
  output [4:0] rt,
  output [4:0] rs,
  output [5:0] op
);


  assign funct = IR[5:0];
  assign imm_16bit = IR[15:0];
  assign imm_26bit = IR[25:0];
  assign op = IR[31:26];
  assign rd = IR[15:11];
  assign rs = IR[25:21];
  assign rt = IR[20:16];
  assign sa = IR[10:6];
endmodule

module type1 (
  input  op0,
  input  op1,
  input  op2,
  input  op3,
  input  op4,
  input  op5,
  input  funct0,
  input  funct1,
  input  funct2,
  input  funct3,
  input  funct4,
  input  funct5,
  output add,
  output addi,
  output addiu,
  output addu,
  output \and ,
  output andi,
  output sll,
  output sra,
  output srl,
  output sub,
  output \or ,
  output ori
);

  wire not_1_out, not_2_out, not_3_out, not_4_out, not_5_out, not_6_out, not_7_out, not_8_out, not_9_out,
       not_10_out, not_11_out, not_12_out, not_13_out, not_14_out, not_15_out, not_16_out, not_17_out,
       not_18_out, not_19_out, not_20_out, not_21_out, not_22_out, not_23_out, not_24_out, not_25_out,
       not_26_out, not_27_out, not_28_out, not_29_out, not_30_out, not_31_out, not_32_out, not_33_out,
       not_34_out, not_35_out, not_36_out, not_37_out, not_38_out, not_39_out, not_40_out, not_41_out,
       not_42_out, not_43_out, not_44_out, not_45_out, not_46_out, not_47_out, not_48_out, not_49_out,
       not_50_out, not_51_out, not_52_out, not_53_out, not_54_out, not_55_out, not_56_out, not_57_out,
       not_58_out, not_59_out, not_60_out, not_61_out, not_62_out, not_63_out, not_64_out, not_65_out,
       not_66_out, not_67_out, not_68_out, not_69_out, not_70_out, not_71_out, not_72_out, not_73_out,
       not_74_out, not_75_out, not_76_out, not_77_out, not_78_out, not_79_out, not_80_out, not_81_out,
       not_82_out, not_83_out, not_84_out, not_85_out, not_86_out, not_87_out, not_88_out, not_89_out,
       not_90_out, not_91_out, not_92_out, not_93_out, not_94_out, not_95_out, not_96_out, not_97_out,
       not_98_out, not_99_out;

  not not_1 (not_1_out, op5);
  not not_2 (not_2_out, op4);
  not not_3 (not_3_out, op3);
  not not_4 (not_4_out, op2);
  not not_5 (not_5_out, op1);
  not not_6 (not_6_out, op0);
  not not_7 (not_7_out, funct4);
  not not_8 (not_8_out, funct3);
  not not_9 (not_9_out, funct2);
  not not_10 (not_10_out, funct1);
  not not_11 (not_11_out, funct0);
  not not_12 (not_12_out, op5);
  not not_13 (not_13_out, op4);
  not not_14 (not_14_out, op2);
  not not_15 (not_15_out, op1);
  not not_16 (not_16_out, op0);
  not not_17 (not_17_out, op5);
  not not_18 (not_18_out, op4);
  not not_19 (not_19_out, op2);
  not not_20 (not_20_out, op1);
  not not_21 (not_21_out, op5);
  not not_22 (not_22_out, op4);
  not not_23 (not_23_out, op3);
  not not_24 (not_24_out, op2);
  not not_25 (not_25_out, op1);
  not not_26 (not_26_out, op0);
  not not_27 (not_27_out, funct4);
  not not_28 (not_28_out, funct3);
  not not_29 (not_29_out, funct2);
  not not_30 (not_30_out, funct1);
  not not_31 (not_31_out, op5);
  not not_32 (not_32_out, op4);
  not not_33 (not_33_out, op3);
  not not_34 (not_34_out, op2);
  not not_35 (not_35_out, op1);
  not not_36 (not_36_out, op0);
  not not_37 (not_37_out, funct4);
  not not_38 (not_38_out, funct3);
  not not_39 (not_39_out, funct1);
  not not_40 (not_40_out, funct0);
  not not_41 (not_41_out, op5);
  not not_42 (not_42_out, op4);
  not not_43 (not_43_out, op1);
  not not_44 (not_44_out, op0);
  not not_45 (not_45_out, op5);
  not not_46 (not_46_out, op4);
  not not_47 (not_47_out, op3);
  not not_48 (not_48_out, op2);
  not not_49 (not_49_out, op1);
  not not_50 (not_50_out, op0);
  not not_51 (not_51_out, funct5);
  not not_52 (not_52_out, funct4);
  not not_53 (not_53_out, funct3);
  not not_54 (not_54_out, funct2);
  not not_55 (not_55_out, funct1);
  not not_56 (not_56_out, funct0);
  not not_57 (not_57_out, op5);
  not not_58 (not_58_out, op4);
  not not_59 (not_59_out, op3);
  not not_60 (not_60_out, op2);
  not not_61 (not_61_out, op1);
  not not_62 (not_62_out, op0);
  not not_63 (not_63_out, funct5);
  not not_64 (not_64_out, funct4);
  not not_65 (not_65_out, funct3);
  not not_66 (not_66_out, funct2);
  not not_67 (not_67_out, op5);
  not not_68 (not_68_out, op4);
  not not_69 (not_69_out, op3);
  not not_70 (not_70_out, op2);
  not not_71 (not_71_out, op1);
  not not_72 (not_72_out, op0);
  not not_73 (not_73_out, funct5);
  not not_74 (not_74_out, funct4);
  not not_75 (not_75_out, funct3);
  not not_76 (not_76_out, funct2);
  not not_77 (not_77_out, funct0);
  not not_78 (not_78_out, op5);
  not not_79 (not_79_out, op4);
  not not_80 (not_80_out, op3);
  not not_81 (not_81_out, op2);
  not not_82 (not_82_out, op1);
  not not_83 (not_83_out, op0);
  not not_84 (not_84_out, funct4);
  not not_85 (not_85_out, funct3);
  not not_86 (not_86_out, funct2);
  not not_87 (not_87_out, funct0);
  not not_88 (not_88_out, op5);
  not not_89 (not_89_out, op4);
  not not_90 (not_90_out, op3);
  not not_91 (not_91_out, op2);
  not not_92 (not_92_out, op1);
  not not_93 (not_93_out, op0);
  not not_94 (not_94_out, funct4);
  not not_95 (not_95_out, funct3);
  not not_96 (not_96_out, funct1);
  not not_97 (not_97_out, op5);
  not not_98 (not_98_out, op4);
  not not_99 (not_99_out, op1);
  and and_1 (add, not_1_out, not_2_out, not_3_out, not_4_out, not_5_out, not_6_out, funct5, not_7_out, not_8_out, not_9_out, not_10_out, not_11_out);
  and and_2 (addi, not_12_out, not_13_out, op3, not_14_out, not_15_out, not_16_out);
  and and_3 (addiu, not_17_out, not_18_out, op3, not_19_out, not_20_out, op0);
  and and_4 (addu, not_21_out, not_22_out, not_23_out, not_24_out, not_25_out, not_26_out, funct5, not_27_out, not_28_out, not_29_out, not_30_out, funct0);
  and and_5 (\and , not_31_out, not_32_out, not_33_out, not_34_out, not_35_out, not_36_out, funct5, not_37_out, not_38_out, funct2, not_39_out, not_40_out);
  and and_6 (andi, not_41_out, not_42_out, op3, op2, not_43_out, not_44_out);
  and and_7 (sll, not_45_out, not_46_out, not_47_out, not_48_out, not_49_out, not_50_out, not_51_out, not_52_out, not_53_out, not_54_out, not_55_out, not_56_out);
  and and_8 (sra, not_57_out, not_58_out, not_59_out, not_60_out, not_61_out, not_62_out, not_63_out, not_64_out, not_65_out, not_66_out, funct1, funct0);
  and and_9 (srl, not_67_out, not_68_out, not_69_out, not_70_out, not_71_out, not_72_out, not_73_out, not_74_out, not_75_out, not_76_out, funct1, not_77_out);
  and and_10 (sub, not_78_out, not_79_out, not_80_out, not_81_out, not_82_out, not_83_out, funct5, not_84_out, not_85_out, not_86_out, funct1, not_87_out);
  and and_11 (\or , not_88_out, not_89_out, not_90_out, not_91_out, not_92_out, not_93_out, funct5, not_94_out, not_95_out, funct2, not_96_out, funct0);
  and and_12 (ori, not_97_out, not_98_out, op3, op2, not_99_out, op0);
endmodule

module type2 (
  input  op0,
  input  op1,
  input  op2,
  input  op3,
  input  op4,
  input  op5,
  input  funct0,
  input  funct1,
  input  funct2,
  input  funct3,
  input  funct4,
  input  funct5,
  output \nor ,
  output lw,
  output sw,
  output beq,
  output bne,
  output slt,
  output slti,
  output sltu,
  output j,
  output jal,
  output jr,
  output syscall
);

  wire not_1_out, not_2_out, not_3_out, not_4_out, not_5_out, not_6_out, not_7_out, not_8_out, not_9_out,
       not_10_out, not_11_out, not_12_out, not_13_out, not_14_out, not_15_out, not_16_out, not_17_out,
       not_18_out, not_19_out, not_20_out, not_21_out, not_22_out, not_23_out, not_24_out, not_25_out,
       not_26_out, not_27_out, not_28_out, not_29_out, not_30_out, not_31_out, not_32_out, not_33_out,
       not_34_out, not_35_out, not_36_out, not_37_out, not_38_out, not_39_out, not_40_out, not_41_out,
       not_42_out, not_43_out, not_44_out, not_45_out, not_46_out, not_47_out, not_48_out, not_49_out,
       not_50_out, not_51_out, not_52_out, not_53_out, not_54_out, not_55_out, not_56_out, not_57_out,
       not_58_out, not_59_out, not_60_out, not_61_out, not_62_out, not_63_out, not_64_out, not_65_out,
       not_66_out, not_67_out, not_68_out, not_69_out, not_70_out, not_71_out, not_72_out, not_73_out;

  not not_1 (not_1_out, op5);
  not not_2 (not_2_out, op4);
  not not_3 (not_3_out, op3);
  not not_4 (not_4_out, op2);
  not not_5 (not_5_out, op1);
  not not_6 (not_6_out, op0);
  not not_7 (not_7_out, funct4);
  not not_8 (not_8_out, funct3);
  not not_9 (not_9_out, op4);
  not not_10 (not_10_out, op3);
  not not_11 (not_11_out, op2);
  not not_12 (not_12_out, op4);
  not not_13 (not_13_out, op2);
  not not_14 (not_14_out, op5);
  not not_15 (not_15_out, op4);
  not not_16 (not_16_out, op3);
  not not_17 (not_17_out, op1);
  not not_18 (not_18_out, op0);
  not not_19 (not_19_out, op5);
  not not_20 (not_20_out, op4);
  not not_21 (not_21_out, op3);
  not not_22 (not_22_out, op1);
  not not_23 (not_23_out, op5);
  not not_24 (not_24_out, op4);
  not not_25 (not_25_out, op3);
  not not_26 (not_26_out, op2);
  not not_27 (not_27_out, op1);
  not not_28 (not_28_out, op0);
  not not_29 (not_29_out, funct4);
  not not_30 (not_30_out, funct2);
  not not_31 (not_31_out, funct0);
  not not_32 (not_32_out, op5);
  not not_33 (not_33_out, op4);
  not not_34 (not_34_out, op2);
  not not_35 (not_35_out, op0);
  not not_36 (not_36_out, op5);
  not not_37 (not_37_out, op4);
  not not_38 (not_38_out, op3);
  not not_39 (not_39_out, op2);
  not not_40 (not_40_out, op1);
  not not_41 (not_41_out, op0);
  not not_42 (not_42_out, funct4);
  not not_43 (not_43_out, funct2);
  not not_44 (not_44_out, op5);
  not not_45 (not_45_out, op4);
  not not_46 (not_46_out, op3);
  not not_47 (not_47_out, op2);
  not not_48 (not_48_out, op0);
  not not_49 (not_49_out, op5);
  not not_50 (not_50_out, op4);
  not not_51 (not_51_out, op3);
  not not_52 (not_52_out, op2);
  not not_53 (not_53_out, op5);
  not not_54 (not_54_out, op4);
  not not_55 (not_55_out, op3);
  not not_56 (not_56_out, op2);
  not not_57 (not_57_out, op1);
  not not_58 (not_58_out, op0);
  not not_59 (not_59_out, funct5);
  not not_60 (not_60_out, funct4);
  not not_61 (not_61_out, funct2);
  not not_62 (not_62_out, funct1);
  not not_63 (not_63_out, funct0);
  not not_64 (not_64_out, op5);
  not not_65 (not_65_out, op4);
  not not_66 (not_66_out, op3);
  not not_67 (not_67_out, op2);
  not not_68 (not_68_out, op1);
  not not_69 (not_69_out, op0);
  not not_70 (not_70_out, funct5);
  not not_71 (not_71_out, funct4);
  not not_72 (not_72_out, funct1);
  not not_73 (not_73_out, funct0);
  and and_1 (\nor , not_1_out, not_2_out, not_3_out, not_4_out, not_5_out, not_6_out, funct5, not_7_out, not_8_out, funct2, funct1, funct0);
  and and_2 (lw, op5, not_9_out, not_10_out, not_11_out, op1, op0);
  and and_3 (sw, op5, not_12_out, op3, not_13_out, op1, op0);
  and and_4 (beq, not_14_out, not_15_out, not_16_out, op2, not_17_out, not_18_out);
  and and_5 (bne, not_19_out, not_20_out, not_21_out, op2, not_22_out, op0);
  and and_6 (slt, not_23_out, not_24_out, not_25_out, not_26_out, not_27_out, not_28_out, funct5, not_29_out, funct3, not_30_out, funct1, not_31_out);
  and and_7 (slti, not_32_out, not_33_out, op3, not_34_out, op1, not_35_out);
  and and_8 (sltu, not_36_out, not_37_out, not_38_out, not_39_out, not_40_out, not_41_out, funct5, not_42_out, funct3, not_43_out, funct1, funct0);
  and and_9 (j, not_44_out, not_45_out, not_46_out, not_47_out, op1, not_48_out);
  and and_10 (jal, not_49_out, not_50_out, not_51_out, not_52_out, op1, op0);
  and and_11 (jr, not_53_out, not_54_out, not_55_out, not_56_out, not_57_out, not_58_out, not_59_out, not_60_out, funct3, not_61_out, not_62_out, not_63_out);
  and and_12 (syscall, not_64_out, not_65_out, not_66_out, not_67_out, not_68_out, not_69_out, not_70_out, not_71_out, funct3, funct2, not_72_out, not_73_out);
endmodule

module type3 (
  input  op0,
  input  op1,
  input  op2,
  input  op3,
  input  op4,
  input  op5,
  input  funct0,
  input  funct1,
  input  funct2,
  input  funct3,
  input  funct4,
  input  funct5,
  output srav,
  output \xor ,
  output sh,
  output bgtz,
  output eret
);

  wire not_1_out, not_2_out, not_3_out, not_4_out, not_5_out, not_6_out, not_7_out, not_8_out, not_9_out,
       not_10_out, not_11_out, not_12_out, not_13_out, not_14_out, not_15_out, not_16_out, not_17_out,
       not_18_out, not_19_out, not_20_out, not_21_out, not_22_out, not_23_out, not_24_out, not_25_out,
       not_26_out, not_27_out, not_28_out, not_29_out, not_30_out, not_31_out, not_32_out, not_33_out;

  not not_1 (not_1_out, op5);
  not not_2 (not_2_out, op4);
  not not_3 (not_3_out, op3);
  not not_4 (not_4_out, op2);
  not not_5 (not_5_out, op1);
  not not_6 (not_6_out, op0);
  not not_7 (not_7_out, funct5);
  not not_8 (not_8_out, funct4);
  not not_9 (not_9_out, funct3);
  not not_10 (not_10_out, op5);
  not not_11 (not_11_out, op4);
  not not_12 (not_12_out, op3);
  not not_13 (not_13_out, op2);
  not not_14 (not_14_out, op1);
  not not_15 (not_15_out, op0);
  not not_16 (not_16_out, funct4);
  not not_17 (not_17_out, funct3);
  not not_18 (not_18_out, funct0);
  not not_19 (not_19_out, op4);
  not not_20 (not_20_out, op2);
  not not_21 (not_21_out, op1);
  not not_22 (not_22_out, op5);
  not not_23 (not_23_out, op4);
  not not_24 (not_24_out, op3);
  not not_25 (not_25_out, op5);
  not not_26 (not_26_out, op3);
  not not_27 (not_27_out, op2);
  not not_28 (not_28_out, op1);
  not not_29 (not_29_out, op0);
  not not_30 (not_30_out, funct5);
  not not_31 (not_31_out, funct2);
  not not_32 (not_32_out, funct1);
  not not_33 (not_33_out, funct0);
  and and_1 (srav, not_1_out, not_2_out, not_3_out, not_4_out, not_5_out, not_6_out, not_7_out, not_8_out, not_9_out, funct2, funct1, funct0);
  and and_2 (\xor , not_10_out, not_11_out, not_12_out, not_13_out, not_14_out, not_15_out, funct5, not_16_out, not_17_out, funct2, funct1, not_18_out);
  and and_3 (sh, op5, not_19_out, op3, not_20_out, not_21_out, op0);
  and and_4 (bgtz, not_22_out, not_23_out, not_24_out, op2, op1, op0);
  and and_5 (eret, not_25_out, op4, not_26_out, not_27_out, not_28_out, not_29_out, not_30_out, funct4, funct3, not_31_out, not_32_out, not_33_out);
endmodule

module type0 (
  input  op0,
  input  op1,
  input  op2,
  input  op3,
  input  op4,
  input  op5,
  input  rs0,
  input  rs1,
  input  rs2,
  input  rs3,
  input  rs4,
  output mfc0,
  output mtc0
);

  wire not_1_out, not_2_out, not_3_out, not_4_out, not_5_out, not_6_out, not_7_out, not_8_out, not_9_out,
       not_10_out, not_11_out, not_12_out, not_13_out, not_14_out, not_15_out, not_16_out, not_17_out,
       not_18_out, not_19_out;

  not not_1 (not_1_out, op5);
  not not_2 (not_2_out, op3);
  not not_3 (not_3_out, op2);
  not not_4 (not_4_out, op1);
  not not_5 (not_5_out, op0);
  not not_6 (not_6_out, rs4);
  not not_7 (not_7_out, rs3);
  not not_8 (not_8_out, rs2);
  not not_9 (not_9_out, rs1);
  not not_10 (not_10_out, rs0);
  not not_11 (not_11_out, op5);
  not not_12 (not_12_out, op3);
  not not_13 (not_13_out, op2);
  not not_14 (not_14_out, op1);
  not not_15 (not_15_out, op0);
  not not_16 (not_16_out, rs4);
  not not_17 (not_17_out, rs3);
  not not_18 (not_18_out, rs1);
  not not_19 (not_19_out, rs0);
  and and_1 (mfc0, not_1_out, op4, not_2_out, not_3_out, not_4_out, not_5_out, not_6_out, not_7_out, not_8_out, not_9_out, not_10_out);
  and and_2 (mtc0, not_11_out, op4, not_12_out, not_13_out, not_14_out, not_15_out, not_16_out, not_17_out, rs2, not_18_out, not_19_out);
endmodule

module IF_ID (
  input  clk,
  input  clr,
  input  EN,
  input  [31:0] F_I,
  input  [31:0] F_PC_4,
  input  [31:0] F_cp0data,
  output [31:0] D_I,
  output [31:0] D_PC_4,
  output [31:0] D_cp0data
);

  wire and_1_out, not_1_out, not_2_out, register_4_q, undriven;

  not not_1 (not_1_out, EN);
  and and_1 (and_1_out, clk, clr);
  Register #(.width(32)) register_1 (.D(F_I), .en(not_1_out), .Q(D_I), .clk(clk), .clr(and_1_out));
  Register #(.width(32)) register_2 (.D(F_PC_4), .en(not_1_out), .Q(D_PC_4), .clk(clk), .clr(and_1_out));
  Register #(.width(32)) register_3 (.D(F_cp0data), .en(not_1_out), .Q(D_cp0data), .clk(clk), .clr(and_1_out));
  Register #(.width(1)) register_4 (.D(1'b1), .en(1'b1), .Q(register_4_q), .clk(undriven), .clr(not_2_out));
  // NOT_Gate not_2 has open pins: in=open, out=not_2_out
endmodule

module ID_EX (
  input  clr,
  input  clk,
  input  D_j,
  input  D_jal,
  input  D_MemtoReg,
  input  D_MemWrite,
  input  D_beq,
  input  D_bne,
  input  D_bgtz,
  input  D_sh,
  input  [31:0] D_R1,
  input  [31:0] D_R2,
  input  [31:0] D_shamt,
  input  [31:0] D_imm,
  input  [31:0] D_pc_4,
  input  [31:0] D_offset,
  input  [31:0] D_cp0data,
  input  [4:0] D_rd,
  input  D_mtc0,
  input  [3:0] D_ALUCTR,
  input  [4:0] D_RW,
  input  D_RegWrite,
  input  D_syscall,
  input  D_shift,
  input  D_ALUSrc,
  input  D_mfc0,
  input  D_sel1,
  input  D_sel2,
  input  D_ERs,
  input  D_MRs,
  input  D_ERt,
  input  D_MRt,
  input  D_jr,
  input  D_lw,
  output E_j,
  output E_jal,
  output E_MemtoReg,
  output E_MemWrite,
  output E_beq,
  output E_bne,
  output E_bgtz,
  output E_sh,
  output [31:0] E_R1,
  output [31:0] E_R2,
  output [31:0] E_shamt,
  output [31:0] E_imm,
  output [31:0] E_pc_4,
  output [31:0] E_offset,
  output [31:0] E_cp0data,
  output [4:0] E_rd,
  output E_mtc0,
  output [3:0] E_ALUCTR,
  output [4:0] E_RW,
  output E_RegWrite,
  output E_syscall,
  output E_shift,
  output E_ALUSrc,
  output E_mfc0,
  output E_sel1,
  output E_sel2,
  output E_ERs,
  output E_MRs,
  output E_ERt,
  output E_MRt,
  output E_jr,
  output E_lw
);

  wire and_1_out, not_1_out, register_12_q, undriven;

  D_Flip_Flop d_ff_1 (.clk(clk), .D(D_j), .Q(E_j), .preset(1'b0), .en(1'b1), .reset(and_1_out));  // open: Qn
  D_Flip_Flop d_ff_2 (.clk(clk), .D(D_jal), .Q(E_jal), .preset(1'b0), .en(1'b1), .reset(and_1_out));  // open: Qn
  D_Flip_Flop d_ff_3 (
    .clk(clk), .D(D_MemtoReg), .Q(E_MemtoReg), .preset(1'b0), .en(1'b1), .reset(and_1_out));  // open: Qn
  D_Flip_Flop d_ff_4 (
    .clk(clk), .D(D_MemWrite), .Q(E_MemWrite), .preset(1'b0), .en(1'b1), .reset(and_1_out));  // open: Qn
  D_Flip_Flop d_ff_5 (.clk(clk), .D(D_beq), .Q(E_beq), .preset(1'b0), .en(1'b1), .reset(and_1_out));  // open: Qn
  D_Flip_Flop d_ff_6 (.clk(clk), .D(D_bne), .Q(E_bne), .preset(1'b0), .en(1'b1), .reset(and_1_out));  // open: Qn
  D_Flip_Flop d_ff_7 (.clk(clk), .D(D_bgtz), .Q(E_bgtz), .preset(1'b0), .en(1'b1), .reset(and_1_out));  // open: Qn
  D_Flip_Flop d_ff_8 (.clk(clk), .D(D_sh), .Q(E_sh), .preset(1'b0), .en(1'b1), .reset(and_1_out));  // open: Qn
  Register #(.width(32)) register_1 (.D(D_R1), .en(1'b1), .Q(E_R1), .clk(clk), .clr(and_1_out));
  Register #(.width(32)) register_2 (.D(D_R2), .en(1'b1), .Q(E_R2), .clk(clk), .clr(and_1_out));
  Register #(.width(32)) register_3 (.D(D_shamt), .en(1'b1), .Q(E_shamt), .clk(clk), .clr(and_1_out));
  Register #(.width(32)) register_4 (.D(D_imm), .en(1'b1), .Q(E_imm), .clk(clk), .clr(and_1_out));
  Register #(.width(32)) register_5 (.D(D_pc_4), .en(1'b1), .Q(E_pc_4), .clk(clk), .clr(and_1_out));
  Register #(.width(32)) register_6 (.D(D_offset), .en(1'b1), .Q(E_offset), .clk(clk), .clr(and_1_out));
  Register #(.width(32)) register_7 (.D(D_cp0data), .en(1'b1), .Q(E_cp0data), .clk(clk), .clr(and_1_out));
  Register #(.width(5)) register_8 (.D(D_rd), .en(1'b1), .Q(E_rd), .clk(clk), .clr(and_1_out));
  Register #(.width(1)) register_9 (.D(D_mtc0), .en(1'b1), .Q(E_mtc0), .clk(clk), .clr(and_1_out));
  Register #(.width(4)) register_10 (.D(D_ALUCTR), .en(1'b1), .Q(E_ALUCTR), .clk(clk), .clr(and_1_out));
  Register #(.width(5)) register_11 (.D(D_RW), .en(1'b1), .Q(E_RW), .clk(clk), .clr(and_1_out));
  D_Flip_Flop d_ff_9 (
    .clk(clk), .D(D_RegWrite), .Q(E_RegWrite), .preset(1'b0), .en(1'b1), .reset(and_1_out));  // open: Qn
  D_Flip_Flop d_ff_10 (
    .clk(clk), .D(D_syscall), .Q(E_syscall), .preset(1'b0), .en(1'b1), .reset(and_1_out));  // open: Qn
  D_Flip_Flop d_ff_11 (.clk(clk), .D(D_shift), .Q(E_shift), .preset(1'b0), .en(1'b1), .reset(and_1_out));  // open: Qn
  D_Flip_Flop d_ff_12 (.clk(clk), .D(D_ALUSrc), .Q(E_ALUSrc), .preset(1'b0), .en(1'b1), .reset(and_1_out));  // open: Qn
  D_Flip_Flop d_ff_13 (.clk(clk), .D(D_mfc0), .Q(E_mfc0), .preset(1'b0), .en(1'b1), .reset(and_1_out));  // open: Qn
  D_Flip_Flop d_ff_14 (.clk(clk), .D(D_sel1), .Q(E_sel1), .preset(1'b0), .en(1'b1), .reset(and_1_out));  // open: Qn
  D_Flip_Flop d_ff_15 (.clk(clk), .D(D_sel2), .Q(E_sel2), .preset(1'b0), .en(1'b1), .reset(and_1_out));  // open: Qn
  D_Flip_Flop d_ff_16 (.clk(clk), .D(D_ERs), .Q(E_ERs), .preset(1'b0), .en(1'b1), .reset(and_1_out));  // open: Qn
  D_Flip_Flop d_ff_17 (.clk(clk), .D(D_MRs), .Q(E_MRs), .preset(1'b0), .en(1'b1), .reset(and_1_out));  // open: Qn
  D_Flip_Flop d_ff_18 (.clk(clk), .D(D_ERt), .Q(E_ERt), .preset(1'b0), .en(1'b1), .reset(and_1_out));  // open: Qn
  D_Flip_Flop d_ff_19 (.clk(clk), .D(D_MRt), .Q(E_MRt), .preset(1'b0), .en(1'b1), .reset(and_1_out));  // open: Qn
  D_Flip_Flop d_ff_20 (.clk(clk), .D(D_jr), .Q(E_jr), .preset(1'b0), .en(1'b1), .reset(and_1_out));  // open: Qn
  D_Flip_Flop d_ff_21 (.clk(clk), .D(D_lw), .Q(E_lw), .preset(1'b0), .en(1'b1), .reset(and_1_out));  // open: Qn
  and and_1 (and_1_out, clk, clr);
  // NOT_Gate not_1 has open pins: in=open, out=not_1_out
  Register #(.width(1)) register_12 (.D(1'b1), .en(1'b1), .Q(register_12_q), .clk(undriven), .clr(not_1_out));
endmodule

module EX_MEM (
  input  clk,
  input  E_jal,
  input  E_mfc0,
  input  E_MemtoReg,
  input  E_MemWrite,
  input  E_sh,
  input  [31:0] E_R2,
  input  [31:0] E_pc_4,
  input  [31:0] E_R,
  input  [31:0] E_cp0data,
  input  [4:0] E_RW,
  input  [4:0] E_rd,
  input  E_mtc0,
  input  E_RegWrite,
  input  E_syscall,
  output M_jal,
  output M_mfc0,
  output M_MemtoReg,
  output M_MemWrite,
  output M_sh,
  output [31:0] M_R2,
  output [31:0] M_pc_4,
  output [31:0] M_R,
  output [31:0] M_cp0data,
  output [4:0] M_RW,
  output [4:0] M_rd,
  output M_mtc0,
  output M_RegWrite,
  output M_syscall
);

  D_Flip_Flop d_ff_1 (.clk(clk), .D(E_jal), .Q(M_jal), .preset(1'b0), .en(1'b1), .reset(1'b0));  // open: Qn
  D_Flip_Flop d_ff_2 (.clk(clk), .D(E_mfc0), .Q(M_mfc0), .preset(1'b0), .en(1'b1), .reset(1'b0));  // open: Qn
  D_Flip_Flop d_ff_3 (.clk(clk), .D(E_MemtoReg), .Q(M_MemtoReg), .preset(1'b0), .en(1'b1), .reset(1'b0));  // open: Qn
  D_Flip_Flop d_ff_4 (.clk(clk), .D(E_MemWrite), .Q(M_MemWrite), .preset(1'b0), .en(1'b1), .reset(1'b0));  // open: Qn
  D_Flip_Flop d_ff_5 (.clk(clk), .D(E_sh), .Q(M_sh), .preset(1'b0), .en(1'b1), .reset(1'b0));  // open: Qn
  Register #(.width(32)) register_1 (.D(E_R2), .en(1'b1), .Q(M_R2), .clk(clk), .clr(1'b0));
  Register #(.width(32)) register_2 (.D(E_pc_4), .en(1'b1), .Q(M_pc_4), .clk(clk), .clr(1'b0));
  Register #(.width(32)) register_3 (.D(E_R), .en(1'b1), .Q(M_R), .clk(clk), .clr(1'b0));
  Register #(.width(32)) register_4 (.D(E_cp0data), .en(1'b1), .Q(M_cp0data), .clk(clk), .clr(1'b0));
  Register #(.width(5)) register_5 (.D(E_RW), .en(1'b1), .Q(M_RW), .clk(clk), .clr(1'b0));
  Register #(.width(5)) register_6 (.D(E_rd), .en(1'b1), .Q(M_rd), .clk(clk), .clr(1'b0));
  Register #(.width(1)) register_7 (.D(E_mtc0), .en(1'b1), .Q(M_mtc0), .clk(clk), .clr(1'b0));
  D_Flip_Flop d_ff_6 (.clk(clk), .D(E_RegWrite), .Q(M_RegWrite), .preset(1'b0), .en(1'b1), .reset(1'b0));  // open: Qn
  D_Flip_Flop d_ff_7 (.clk(clk), .D(E_syscall), .Q(M_syscall), .preset(1'b0), .en(1'b1), .reset(1'b0));  // open: Qn
endmodule

module MEM_WB (
  input  clk,
  input  M_RegWrite,
  input  M_MemtoReg,
  input  [4:0] M_RW,
  input  [31:0] M_R,
  input  [31:0] M_D,
  input  [31:0] M_PC_4,
  input  [31:0] M_cp0data,
  input  [4:0] M_rd,
  input  M_mtc0,
  input  M_mfc0,
  input  M_jal,
  input  M_syscall,
  output W_RegWrite,
  output W_MemtoReg,
  output [4:0] W_RW,
  output [31:0] W_R,
  output [31:0] W_D,
  output [31:0] W_PC_4,
  output [31:0] W_cp0data,
  output [4:0] W_rd,
  output W_mtc0,
  output W_mfc0,
  output W_jal,
  output W_syscall
);

  D_Flip_Flop d_ff_1 (.clk(clk), .D(M_RegWrite), .Q(W_RegWrite), .preset(1'b0), .en(1'b1), .reset(1'b0));  // open: Qn
  D_Flip_Flop d_ff_2 (.clk(clk), .D(M_MemtoReg), .Q(W_MemtoReg), .preset(1'b0), .en(1'b1), .reset(1'b0));  // open: Qn
  Register #(.width(5)) register_1 (.D(M_RW), .en(1'b1), .Q(W_RW), .clk(clk), .clr(1'b0));
  Register #(.width(32)) register_2 (.D(M_R), .en(1'b1), .Q(W_R), .clk(clk), .clr(1'b0));
  Register #(.width(32)) register_3 (.D(M_D), .en(1'b1), .Q(W_D), .clk(clk), .clr(1'b0));
  Register #(.width(32)) register_4 (.D(M_PC_4), .en(1'b1), .Q(W_PC_4), .clk(clk), .clr(1'b0));
  Register #(.width(32)) register_5 (.D(M_cp0data), .en(1'b1), .Q(W_cp0data), .clk(clk), .clr(1'b0));
  Register #(.width(5)) register_6 (.D(M_rd), .en(1'b1), .Q(W_rd), .clk(clk), .clr(1'b0));
  Register #(.width(1)) register_7 (.D(M_mtc0), .en(1'b1), .Q(W_mtc0), .clk(clk), .clr(1'b0));
  D_Flip_Flop d_ff_3 (.clk(clk), .D(M_mfc0), .Q(W_mfc0), .preset(1'b0), .en(1'b1), .reset(1'b0));  // open: Qn
  D_Flip_Flop d_ff_4 (.clk(clk), .D(M_jal), .Q(W_jal), .preset(1'b0), .en(1'b1), .reset(1'b0));  // open: Qn
  D_Flip_Flop d_ff_5 (.clk(clk), .D(M_syscall), .Q(W_syscall), .preset(1'b0), .en(1'b1), .reset(1'b0));  // open: Qn
endmodule

module Hazard_Unit (
  input  E_j,
  input  branch,
  input  [4:0] Rt,
  input  [4:0] Rs,
  input  M_RegWrite,
  input  E_RegWrite,
  input  E_jr,
  input  readRs,
  input  E_LW,
  input  [4:0] E_RW,
  input  clk,
  input  [4:0] M_RW,
  input  readRt,
  output BRANCH_2,
  output E_Rs,
  output LOADUSE,
  output M_Rs,
  output E_Rt,
  output M_Rt
);

  wire and_5_out, comparator_1_eq, comparator_2_eq, comparator_3_eq, comparator_4_eq, comparator_5_eq,
       comparator_6_eq, or_1_out, or_2_out;

  Comparator #(.width(5), .mode("unsigned")) comparator_1 (
    .a({5{1'b0}}), .b(Rs), .eq(comparator_1_eq));  // open: gt, lt
  Comparator #(.width(5), .mode("unsigned")) comparator_2 (.a(Rs), .b(E_RW), .eq(comparator_2_eq));  // open: gt, lt
  Comparator #(.width(5), .mode("unsigned")) comparator_3 (.a(Rs), .b(M_RW), .eq(comparator_3_eq));  // open: gt, lt
  Comparator #(.width(5), .mode("unsigned")) comparator_4 (
    .a({5{1'b0}}), .b(Rt), .eq(comparator_4_eq));  // open: gt, lt
  Comparator #(.width(5), .mode("unsigned")) comparator_5 (.a(Rt), .b(E_RW), .eq(comparator_5_eq));  // open: gt, lt
  Comparator #(.width(5), .mode("unsigned")) comparator_6 (.a(Rt), .b(M_RW), .eq(comparator_6_eq));  // open: gt, lt
  and and_1 (E_Rs, E_RegWrite, readRs, ~comparator_1_eq, comparator_2_eq);  // AND_Gate
  and and_2 (M_Rs, M_RegWrite, readRs, ~comparator_1_eq, comparator_3_eq);  // AND_Gate
  and and_3 (E_Rt, E_RegWrite, readRt, ~comparator_4_eq, comparator_5_eq);  // AND_Gate
  and and_4 (M_Rt, M_RegWrite, readRt, ~comparator_4_eq, comparator_6_eq);  // AND_Gate
  or or_1 (or_1_out, E_j, branch, E_jr);
  and and_5 (and_5_out, E_LW, or_2_out);
  or or_2 (or_2_out, E_Rs, E_Rt);
  Register #(.width(1), .trigger("falling")) register_1 (.D(or_1_out), .en(1'b1), .Q(BRANCH_2), .clk(clk), .clr(1'b0));
  Register #(.width(1), .trigger("falling")) register_2 (.D(and_5_out), .en(1'b1), .Q(LOADUSE), .clk(clk), .clr(1'b0));
endmodule
