// Logisim project CS1409_U201414797_张丹朱_regfile.circ as structural Verilog: 3 circuits, main circuit main
module main (
  input  [4:0] Reg1_num,
  input  [4:0] Reg2,
  input  [4:0] Write_Reg_num,
  input  [31:0] Din,
  input  Write_Enable,
  input  Clock,
  output [31:0] Reg1,
  output [31:0] s0_Value,
  output [31:0] s1_Value,
  output [31:0] s2_Value,
  output [31:0] ra_Value,
  output [31:0] Reg2_2,
  output [31:0] v0,
  output [31:0] a0
);

  wire [31:0] demultiplexer_1_out0, regs_1_r0, regs_1_r1, regs_1_r3, regs_1_r5, regs_1_r6, regs_1_r7,
       regs_1_r8, regs_1_r9, regs_1_r10, regs_1_r11, regs_1_r12, regs_1_r13, regs_1_r14, regs_1_r15,
       regs_1_r19, regs_1_r20, regs_1_r21, regs_1_r22, regs_1_r23, regs_1_r24, regs_1_r25, regs_1_r26,
       regs_1_r27, regs_1_r28, regs_1_r29, regs_1_r30;

  // Probe on Reg1_num
  // Probe on Reg2
  // Probe on Write_Reg_num
  // Probe on Din
  // Probe on Din
  // Probe on Write_Enable
  Demultiplexer #(.select(5), .enable("false")) demultiplexer_1 (
    .out0(demultiplexer_1_out0[0]), .out1(demultiplexer_1_out0[1]), .out2(demultiplexer_1_out0[2]),
    .out3(demultiplexer_1_out0[3]), .out4(demultiplexer_1_out0[4]), .out5(demultiplexer_1_out0[5]),
    .out6(demultiplexer_1_out0[6]), .out7(demultiplexer_1_out0[7]), .out8(demultiplexer_1_out0[8]),
    .out9(demultiplexer_1_out0[9]), .out10(demultiplexer_1_out0[10]), .out11(demultiplexer_1_out0[11]),
    .out12(demultiplexer_1_out0[12]), .out13(demultiplexer_1_out0[13]), .out14(demultiplexer_1_out0[14]),
    .out15(demultiplexer_1_out0[15]), .out16(demultiplexer_1_out0[16]), .out17(demultiplexer_1_out0[17]),
    .out18(demultiplexer_1_out0[18]), .out19(demultiplexer_1_out0[19]), .out20(demultiplexer_1_out0[20]),
    .out21(demultiplexer_1_out0[21]), .out22(demultiplexer_1_out0[22]), .out23(demultiplexer_1_out0[23]),
    .out24(demultiplexer_1_out0[24]), .out25(demultiplexer_1_out0[25]), .out26(demultiplexer_1_out0[26]),
    .out27(demultiplexer_1_out0[27]), .out28(demultiplexer_1_out0[28]), .out29(demultiplexer_1_out0[29]),
    .out30(demultiplexer_1_out0[30]), .out31(demultiplexer_1_out0[31]), .in(Write_Enable), .sel(Write_Reg_num));
  // Probe on Reg1
  // Probe on Reg1
  // Probe on Reg2_2
  // Probe on Reg2_2
  regs regs_1 (
    .WE(demultiplexer_1_out0), .R0(regs_1_r0), .R1(regs_1_r1), .R2(v0), .R3(regs_1_r3), .R4(a0),
    .R5(regs_1_r5), .R6(regs_1_r6), .R7(regs_1_r7), .R8(regs_1_r8), .R9(regs_1_r9), .R10(regs_1_r10),
    .R11(regs_1_r11), .R12(regs_1_r12), .R13(regs_1_r13), .R14(regs_1_r14), .R15(regs_1_r15), .R16(s0_Value),
    .R17(s1_Value), .R18(s2_Value), .R19(regs_1_r19), .R20(regs_1_r20), .R21(regs_1_r21), .R22(regs_1_r22),
    .R23(regs_1_r23), .R24(regs_1_r24), .R25(regs_1_r25), .R26(regs_1_r26), .R27(regs_1_r27),
    .R28(regs_1_r28), .R29(regs_1_r29), .R30(regs_1_r30), .R31(ra_Value), .clk(Clock), .Din(Din));
  // Probe on s0_Value
  // Probe on s0_Value
  // Probe on s1_Value
  // Probe on s1_Value
  Multiplexer #(.select(5), .width(32), .enable("false")) multiplexer_1 (
    .in0(regs_1_r0), .in1(regs_1_r1), .in2(v0), .in3(regs_1_r3), .in4(a0), .in5(regs_1_r5), .in6(regs_1_r6),
    .in7(regs_1_r7), .in8(regs_1_r8), .in9(regs_1_r9), .in10(regs_1_r10), .in11(regs_1_r11),
    .in12(regs_1_r12), .in13(regs_1_r13), .in14(regs_1_r14), .in15(regs_1_r15), .in16(s0_Value),
    .in17(s1_Value), .in18(s2_Value), .in19(regs_1_r19), .in20(regs_1_r20), .in21(regs_1_r21),
    .in22(regs_1_r22), .in23(regs_1_r23), .in24(regs_1_r24), .in25(regs_1_r25), .in26(regs_1_r26),
    .in27(regs_1_r27), .in28(regs_1_r28), .in29(regs_1_r29), .in30(regs_1_r30), .in31(ra_Value),
    .out(Reg2_2), .sel(Reg2));
  // Probe on s2_Value
  // Probe on s2_Value
  // Probe on ra_Value
  // Probe on ra_Value
  Multiplexer #(.select(5), .width(32), .enable("false")) multiplexer_2 (
    .in0(regs_1_r0), .in1(regs_1_r1), .in2(v0), .in3(regs_1_r3), .in4(a0), .in5(regs_1_r5), .in6(regs_1_r6),
    .in7(regs_1_r7), .in8(regs_1_r8), .in9(regs_1_r9), .in10(regs_1_r10), .in11(regs_1_r11),
    .in12(regs_1_r12), .in13(regs_1_r13), .in14(regs_1_r14), .in15(regs_1_r15), .in16(s0_Value),
    .in17(s1_Value), .in18(s2_Value), .in19(regs_1_r19), .in20(regs_1_r20), .in21(regs_1_r21),
    .in22(regs_1_r22), .in23(regs_1_r23), .in24(regs_1_r24), .in25(regs_1_r25), .in26(regs_1_r26),
    .in27(regs_1_r27), .in28(regs_1_r28), .in29(regs_1_r29), .in30(regs_1_r30), .in31(ra_Value), .out(Reg1),
    .sel(Reg1_num));

  // Other names for the same wires on the sheet: clk = Clock; ra[31:0] = ra_Value; reg2_num[4:0] = Reg2;
  //   reg2_t[31:0] = Reg2_2; s0[31:0] = s0_Value; s1[31:0] = s1_Value; s2[31:0] = s2_Value; WE = Write_Enable;
  //   write_data[31:0] = Din

  // Notes on the sheet:
  //   输入引脚
  //   输出引脚
  //   Debug引脚，便于观测寄存器值
  //   请勿修改引脚以及封装，直接使用隧道连接电路
endmodule

// REGS
module regs (
  input  [31:0] Din,
  input  [31:0] WE,
  input  clk,
  output [31:0] R0,
  output [31:0] R1,
  output [31:0] R2,
  output [31:0] R3,
  output [31:0] R4,
  output [31:0] R5,
  output [31:0] R6,
  output [31:0] R7,
  output [31:0] R8,
  output [31:0] R9,
  output [31:0] R10,
  output [31:0] R11,
  output [31:0] R12,
  output [31:0] R13,
  output [31:0] R14,
  output [31:0] R15,
  output [31:0] R16,
  output [31:0] R17,
  output [31:0] R18,
  output [31:0] R19,
  output [31:0] R20,
  output [31:0] R21,
  output [31:0] R22,
  output [31:0] R23,
  output [31:0] R24,
  output [31:0] R25,
  output [31:0] R26,
  output [31:0] R27,
  output [31:0] R28,
  output [31:0] R29,
  output [31:0] R30,
  output [31:0] R31
);

  Register #(.width(32), .trigger("falling")) register_1 (.D({32{1'b0}}), .en(WE[0]), .Q(R0), .clk(clk), .clr(1'b0));
  Register #(.width(32), .trigger("falling")) register_2 (.D(Din), .en(WE[8]), .Q(R8), .clk(clk), .clr(1'b0));
  Register #(.width(32), .trigger("falling")) register_3 (.D(Din), .en(WE[16]), .Q(R16), .clk(clk), .clr(1'b0));
  Register #(.width(32), .trigger("falling")) register_4 (.D(Din), .en(WE[24]), .Q(R24), .clk(clk), .clr(1'b0));
  Register #(.width(32), .trigger("falling")) register_5 (.D(Din), .en(WE[1]), .Q(R1), .clk(clk), .clr(1'b0));
  Register #(.width(32), .trigger("falling")) register_6 (.D(Din), .en(WE[9]), .Q(R9), .clk(clk), .clr(1'b0));
  Register #(.width(32), .trigger("falling")) register_7 (.D(Din), .en(WE[17]), .Q(R17), .clk(clk), .clr(1'b0));
  Register #(.width(32), .trigger("falling")) register_8 (.D(Din), .en(WE[25]), .Q(R25), .clk(clk), .clr(1'b0));
  Register #(.width(32), .trigger("falling")) register_9 (.D(Din), .en(WE[2]), .Q(R2), .clk(clk), .clr(1'b0));
  Register #(.width(32), .trigger("falling")) register_10 (.D(Din), .en(WE[10]), .Q(R10), .clk(clk), .clr(1'b0));
  Register #(.width(32), .trigger("falling")) register_11 (.D(Din), .en(WE[18]), .Q(R18), .clk(clk), .clr(1'b0));
  Register #(.width(32), .trigger("falling")) register_12 (.D(Din), .en(WE[26]), .Q(R26), .clk(clk), .clr(1'b0));
  Register #(.width(32), .trigger("falling")) register_13 (.D(Din), .en(WE[3]), .Q(R3), .clk(clk), .clr(1'b0));
  Register #(.width(32), .trigger("falling")) register_14 (.D(Din), .en(WE[11]), .Q(R11), .clk(clk), .clr(1'b0));
  Register #(.width(32), .trigger("falling")) register_15 (.D(Din), .en(WE[19]), .Q(R19), .clk(clk), .clr(1'b0));
  Register #(.width(32), .trigger("falling")) register_16 (.D(Din), .en(WE[27]), .Q(R27), .clk(clk), .clr(1'b0));
  Register #(.width(32), .trigger("falling")) register_17 (.D(Din), .en(WE[4]), .Q(R4), .clk(clk), .clr(1'b0));
  Register #(.width(32), .trigger("falling")) register_18 (.D(Din), .en(WE[12]), .Q(R12), .clk(clk), .clr(1'b0));
  Register #(.width(32), .trigger("falling")) register_19 (.D(Din), .en(WE[20]), .Q(R20), .clk(clk), .clr(1'b0));
  Register #(.width(32), .trigger("falling")) register_20 (.D(Din), .en(WE[28]), .Q(R28), .clk(clk), .clr(1'b0));
  Register #(.width(32), .trigger("falling")) register_21 (.D(Din), .en(WE[5]), .Q(R5), .clk(clk), .clr(1'b0));
  Register #(.width(32), .trigger("falling")) register_22 (.D(Din), .en(WE[13]), .Q(R13), .clk(clk), .clr(1'b0));
  Register #(.width(32), .trigger("falling")) register_23 (.D(Din), .en(WE[21]), .Q(R21), .clk(clk), .clr(1'b0));
  Register #(.width(32), .trigger("falling")) register_24 (.D(Din), .en(WE[29]), .Q(R29), .clk(clk), .clr(1'b0));
  Register #(.width(32), .trigger("falling")) register_25 (.D(Din), .en(WE[6]), .Q(R6), .clk(clk), .clr(1'b0));
  Register #(.width(32), .trigger("falling")) register_26 (.D(Din), .en(WE[14]), .Q(R14), .clk(clk), .clr(1'b0));
  Register #(.width(32), .trigger("falling")) register_27 (.D(Din), .en(WE[22]), .Q(R22), .clk(clk), .clr(1'b0));
  Register #(.width(32), .trigger("falling")) register_28 (.D(Din), .en(WE[30]), .Q(R30), .clk(clk), .clr(1'b0));
  Register #(.width(32), .trigger("falling")) register_29 (.D(Din), .en(WE[7]), .Q(R7), .clk(clk), .clr(1'b0));
  Register #(.width(32), .trigger("falling")) register_30 (.D(Din), .en(WE[15]), .Q(R15), .clk(clk), .clr(1'b0));
  Register #(.width(32), .trigger("falling")) register_31 (.D(Din), .en(WE[23]), .Q(R23), .clk(clk), .clr(1'b0));
  Register #(.width(32), .trigger("falling")) register_32 (.D(Din), .en(WE[31]), .Q(R31), .clk(clk), .clr(1'b0));
endmodule

module add (
);

  wire clock_1_out, counter_3_carry, demultiplexer_1_out0, demultiplexer_1_out1, demultiplexer_1_out2,
       not_1_out;
  wire [1:0] counter_1_q;
  wire [3:0] main_1_reg2_2_2, main_1_reg2_2_3, main_1_reg2_2_4, main_1_reg2_2_5, main_1_reg2_2_6,
       main_1_reg2_2_7;
  wire [5:0] adder_1_out, counter_2_q, counter_3_q, multiplexer_1_out;
  wire [7:0] main_1_reg2_2;
  wire [31:0] alu_1_p4, ram_1_data;

  Demultiplexer #(.select(2), .enable("false")) demultiplexer_1 (
    .out0(demultiplexer_1_out0), .out1(demultiplexer_1_out1), .out2(demultiplexer_1_out2), .in(1'b1),
    .sel(counter_1_q));  // open: out3
  Counter #(.width(2), .max('h2)) counter_1 (
    .load(1'b0), .D(2'b00), .count(1'b1), .Q(counter_1_q), .clk(clock_1_out), .clr(1'b0));  // open: carry
  Clock clock_1 (.out(clock_1_out));
  Counter #(.width(6), .max('h20), .ongoal("stay")) counter_2 (
    .load(1'b0), .D({6{1'b0}}), .count(1'b1), .Q(counter_2_q), .clk(demultiplexer_1_out0), .clr(1'b0));  // open: carry
  Adder #(.width(6)) adder_1 (.a(6'b100000), .b(counter_2_q), .out(adder_1_out), .cin(1'b0));  // open: cout
  Counter #(.width(6), .max('h20), .ongoal("stay")) counter_3 (
    .load(1'b0), .D({6{1'b0}}), .count(1'b1), .Q(counter_3_q), .carry(counter_3_carry),
    .clk(demultiplexer_1_out2), .clr(1'b0));
  Multiplexer #(.width(6)) multiplexer_1 (
    .in0(adder_1_out), .in1(counter_3_q), .out(multiplexer_1_out), .sel(demultiplexer_1_out0), .en(not_1_out));
  not not_1 (not_1_out, counter_3_carry);
  Hex_Digit_Display hex_digit_display_1 (.value(main_1_reg2_2_7));  // open: dp
  Hex_Digit_Display hex_digit_display_2 (.value(main_1_reg2_2_6));  // open: dp
  Hex_Digit_Display hex_digit_display_3 (.value(main_1_reg2_2_5));  // open: dp
  main main_1 (
    .Reg2(5'b00001), .Write_Reg_num(5'b00001), .Din(alu_1_p4), .Write_Enable(not_1_out),
    .Clock(demultiplexer_1_out1),
    .Reg2_2({main_1_reg2_2_7, main_1_reg2_2_6, main_1_reg2_2_5, main_1_reg2_2_4, main_1_reg2_2_3, main_1_reg2_2_2, main_1_reg2_2}));  // open: Reg1_num, Reg1, s0_Value, s1_Value, s2_Value, ra_Value, v0, a0
  RAM #(.addrWidth(6), .dataWidth(32), .bus("separate")) ram_1 (
    .addr(multiplexer_1_out),
    .din({main_1_reg2_2_7, main_1_reg2_2_6, main_1_reg2_2_5, main_1_reg2_2_4, main_1_reg2_2_3, main_1_reg2_2_2, main_1_reg2_2}),
    .data(ram_1_data), .str(not_1_out), .sel(1'b1), .clk(demultiplexer_1_out2), .ld(1'b1), .clr(1'b0));
  Hex_Digit_Display hex_digit_display_4 (.value(main_1_reg2_2_4));  // open: dp
  Hex_Digit_Display hex_digit_display_5 (.value(main_1_reg2_2_3));  // open: dp
  // ALU alu_1: pin names not known; wires that end beside it: {main_1_reg2_2_7, main_1_reg2_2_6, main_1_reg2_2_5, main_1_reg2_2_4, main_1_reg2_2_3, main_1_reg2_2_2, main_1_reg2_2}, ram_1_data, 4'b0101, alu_1_p4
  Hex_Digit_Display hex_digit_display_6 (.value(main_1_reg2_2_2));  // open: dp
  Hex_Digit_Display hex_digit_display_7 (.value(main_1_reg2_2[3:0]));  // open: dp
  Hex_Digit_Display hex_digit_display_8 (.value(main_1_reg2_2[7:4]));  // open: dp
endmodule
