// Logisim project CS1409_U201414797_张丹朱_cpu.circ as structural Verilog: 7 circuits, main circuit main
module main (
);

  wire alucount, ALUSrc, and_1_out, and_2_out, and_3_out, and_4_out, and_5_out, and_7_out, and_8_out,
       and_9_out, and_10_out, and_11_out, and_12_out, and_13_out, and_15_out, beq, bgtz, bne, clk,
       clock_1_out, comparator_1_eq, demultiplexer_2_out1, demultiplexer_2_out2, demultiplexer_2_out3,
       demultiplexer_3_out1, demultiplexer_3_out2, demultiplexer_3_out3, eret, halt, highlow, I0, I1, I2, IE,
       IS, IS0, ISRC0_2_out, ISRC1_2_out, ISRC2_2_out, j, jal, jr, less, MentoReg, MenWrite, mfc0, mtc0,
       multiplexer_4_out, not_1_out, not_3_out, not_4_out, not_5_out, or_1_out, or_2_out, or_3_out, or_4_out,
       or_5_out, or_6_out, or_7_out, or_8_out, or_9_out, other, priority_encoder_1_en_out,
       priority_encoder_1_gs, RegDst, RegWrite, sh, shift, srav, syscall, zero;
  wire [1:0] priority_encoder_1_out;
  wire [3:0] adder_1_out_2, ALUControl;
  wire [4:0] di_1_sa, multiplexer_6_out, multiplexer_7_out, rd, rs, rt;
  wire [5:0] funct, op;
  wire [9:0] demultiplexer_1_out0, demultiplexer_1_out1;
  wire [11:0] adder_3_out, adder_4_out, counter_1_q, counter_2_q, counter_3_q, counter_4_q, counter_5_q,
       counter_6_q, finish;
  wire [15:0] di_1_imm_16bit, ram_1_data;
  wire [25:0] di_1_imm_26bit;
  wire [27:0] adder_1_out, bit_extender_2_out, shifter_1_out;
  wire [31:0] a0, adder_2_out, bit_extender_1_out, bit_extender_3_out, bit_extender_4_out, CAUSE_q, cp0data,
       epc, main_1_reg1, main_1_reg2_2, multiplexer_1_out, multiplexer_2_out, multiplexer_3_out,
       multiplexer_5_out, multiplexer_8_out, multiplexer_9_out, multiplexer_10_out, multiplexer_11_out,
       multiplexer_12_out, multiplexer_13_out, multiplexer_14_out, multiplexer_15_out, multiplexer_16_out,
       multiplexer_17_out, multiplexer_18_out, multiplexer_19_out, multiplexer_20_out, multiplexer_22_out,
       pcbuf, register_2_q, register_3_q, rom_1_data, rom_2_data, shifter_2_out, v0;
  wire [31:1] STATUS_q;
  wire [31:2] alu_1_p5;
  wire [31:16] ram_1_data_2;

  Multiplexer #(.width(32), .enable("false")) multiplexer_1 (
    .in0(multiplexer_16_out), .in1(main_1_reg1), .out(multiplexer_1_out), .sel(jr));
  Multiplexer #(.width(32), .enable("false")) multiplexer_2 (
    .in0(multiplexer_1_out), .in1(epc), .out(multiplexer_2_out), .sel(eret));
  Register #(.width(32)) register_1 (.D(multiplexer_2_out), .en(1'b1), .Q(pcbuf), .clk(IS0));  // open: clr
  Multiplexer #(.width(32), .enable("false")) multiplexer_3 (
    .in0(multiplexer_2_out), .in1(32'h80000000), .out(multiplexer_3_out), .sel(IS));
  Register #(.width(32)) register_2 (
    .D(multiplexer_3_out), .en(halt), .Q(register_2_q), .clk(multiplexer_4_out), .clr(1'b0));
  Multiplexer #(.enable("false")) multiplexer_4 (.in0(clk), .in1(not_1_out), .out(multiplexer_4_out), .sel(IS));
  not not_1 (not_1_out, clk);
  Demultiplexer #(.width(10), .enable("false")) demultiplexer_1 (
    .out0(demultiplexer_1_out0), .out1(demultiplexer_1_out1), .in(register_2_q[11:2]), .sel(register_2_q[31]));
  ROM #(.addrWidth(10), .dataWidth(32)) rom_1 (.addr(demultiplexer_1_out0), .data(rom_1_data), .sel(1'b1));
  ROM #(.addrWidth(10), .dataWidth(32)) rom_2 (.addr(demultiplexer_1_out1), .data(rom_2_data), .sel(1'b1));
  Multiplexer #(.width(32), .enable("false")) multiplexer_5 (
    .in0(rom_1_data), .in1(rom_2_data), .out(multiplexer_5_out), .sel(register_2_q[31]));
  Comparator #(.width(32)) comparator_1 (.a(v0), .b(32'ha), .eq(comparator_1_eq));  // open: gt, lt
  and and_1 (and_1_out, comparator_1_eq, syscall);
  not not_2 (halt, and_1_out);
  DI di_1 (
    .IR(multiplexer_5_out), .imm_26bit(di_1_imm_26bit), .imm_16bit(di_1_imm_16bit), .funct(funct),
    .sa(di_1_sa), .rd(rd), .rt(rt), .rs(rs), .op(op));
  Adder #(.width(32)) adder_1 (.a(register_2_q), .b(32'h4), .out({adder_1_out_2, adder_1_out}));  // open: cin, cout
  and and_2 (and_2_out, syscall, not_3_out);
  not not_3 (not_3_out, comparator_1_eq);
  Register #(.width(32)) register_3 (.D(a0), .en(and_2_out), .Q(register_3_q), .clk(clk), .clr(1'b0));
  ControlUnit ControlUnit (
    .Op(op), .Funct(funct), .MentoReg(MentoReg), .MemWrite(MenWrite), .ALUControl(ALUControl),
    .ALUSrc(ALUSrc), .RegDst(RegDst), .RegWrite(RegWrite), .jr(jr), .j(j), .shift(shift), .beq(beq),
    .bne(bne), .syscall(syscall), .jal(jal), .alucount(alucount), .other_count(other), .srav(srav), .sh(sh),
    .bgtz(bgtz), .Rs(rs), .eret(eret), .mfc0(mfc0), .mtc0(mtc0));
  Multiplexer #(.width(5), .enable("false")) multiplexer_6 (.in0(rt), .in1(rd), .out(multiplexer_6_out), .sel(RegDst));
  Multiplexer #(.width(5), .enable("false")) multiplexer_7 (
    .in0(multiplexer_6_out), .in1({5{1'b1}}), .out(multiplexer_7_out), .sel(jal));
  assign bit_extender_1_out = {{27{1'b0}}, di_1_sa};  // Bit_Extender bit_extender_1
  assign bit_extender_2_out = {{2{di_1_imm_26bit[25]}}, di_1_imm_26bit};  // Bit_Extender bit_extender_2
  Shifter #(.width(28)) shifter_1 (.in(bit_extender_2_out), .\dist (5'b00010), .out(shifter_1_out));
  Hex_Digit_Display hex_digit_display_1 (.value(register_3_q[31:28]));  // open: dp
  Multiplexer #(.width(32), .enable("false")) multiplexer_8 (
    .in0(multiplexer_9_out), .in1(cp0data), .out(multiplexer_8_out), .sel(mfc0));
  Multiplexer #(.width(32), .enable("false")) multiplexer_9 (
    .in0(multiplexer_22_out), .in1({adder_1_out_2, adder_1_out}), .out(multiplexer_9_out), .sel(jal));
  assign bit_extender_3_out = {{16{di_1_imm_16bit[15]}}, di_1_imm_16bit};  // Bit_Extender bit_extender_3
  Hex_Digit_Display hex_digit_display_2 (.value(register_3_q[27:24]));  // open: dp
  Hex_Digit_Display hex_digit_display_3 (.value(register_3_q[23:20]));  // open: dp
  LED ISRC0 (.in(I0));
  \CS1409_U201414797_张丹朱_regfile_main  main_1 (
    .Reg1_num(rs), .Reg2(rt), .Write_Reg_num(multiplexer_7_out), .Din(multiplexer_8_out),
    .Write_Enable(RegWrite), .Clock(clk), .Reg1(main_1_reg1), .Reg2_2(main_1_reg2_2), .v0(v0), .a0(a0));  // open: s0_Value, s1_Value, s2_Value, ra_Value
  Hex_Digit_Display hex_digit_display_4 (.value(register_3_q[15:12]));  // open: dp
  Hex_Digit_Display hex_digit_display_5 (.value(register_3_q[19:16]));  // open: dp
  LED ISRC1 (.in(I1));
  Multiplexer #(.width(32), .enable("false")) multiplexer_10 (
    .in0(main_1_reg2_2), .in1(bit_extender_3_out), .out(multiplexer_10_out), .sel(ALUSrc));
  Shifter #(.width(32)) shifter_2 (.in(bit_extender_3_out), .\dist (5'b00010), .out(shifter_2_out));
  Hex_Digit_Display hex_digit_display_6 (.value(register_3_q[7:4]));  // open: dp
  Hex_Digit_Display hex_digit_display_7 (.value(register_3_q[11:8]));  // open: dp
  LED ISRC2 (.in(I2));
  or or_1 (or_1_out, shift, srav);
  Multiplexer #(.width(32), .enable("false")) multiplexer_11 (
    .in0(main_1_reg1), .in1(main_1_reg2_2), .out(multiplexer_11_out), .sel(or_1_out));
  Multiplexer #(.width(32), .enable("false")) multiplexer_12 (
    .in0(multiplexer_10_out), .in1(bit_extender_1_out), .out(multiplexer_12_out), .sel(shift));
  or or_2 (or_2_out, srav, bgtz);
  Adder #(.width(32)) adder_2 (
    .a(shifter_2_out), .b({adder_1_out_2, adder_1_out}), .out(adder_2_out));  // open: cin, cout
  and and_3 (and_3_out, beq, zero);
  Hex_Digit_Display hex_digit_display_8 (.value(register_3_q[3:0]));  // open: dp
  Multiplexer #(.width(32), .enable("false")) multiplexer_13 (
    .in0(multiplexer_11_out), .in1({32{1'b0}}), .out(multiplexer_13_out), .sel(bgtz));
  Multiplexer #(.width(32), .enable("false")) multiplexer_14 (
    .in0(multiplexer_12_out), .in1(main_1_reg1), .out(multiplexer_14_out), .sel(or_2_out));
  Multiplexer #(.width(32), .enable("false")) multiplexer_15 (
    .in0({adder_1_out_2, adder_1_out}), .in1(adder_2_out), .out(multiplexer_15_out), .sel(or_3_out));
  Multiplexer #(.width(32), .enable("false")) multiplexer_16 (
    .in0(multiplexer_15_out), .in1({adder_1_out_2, shifter_1_out}), .out(multiplexer_16_out), .sel(j));
  or or_3 (or_3_out, and_3_out, and_5_out, and_4_out);
  and and_4 (and_4_out, bgtz, less);
  and and_5 (and_5_out, bne, not_4_out);
  not not_4 (not_4_out, zero);
  Demultiplexer #(.select(2), .enable("false")) demultiplexer_2 (
    .out1(demultiplexer_2_out1), .out2(demultiplexer_2_out2), .out3(demultiplexer_2_out3), .in(1'b1),
    .sel(rd[1:0]));  // open: out0
  and and_6 (clk, clock_1_out, halt);
  Clock clock_1 (.out(clock_1_out));
  // ALU alu_1: pin names not known; wires that end beside it: multiplexer_13_out, multiplexer_14_out, ALUControl, zero, {alu_1_p5, highlow, less}
  and and_7 (and_7_out, demultiplexer_2_out1, mtc0);
  and and_8 (and_8_out, demultiplexer_2_out2, mtc0);
  Multiplexer #(.width(32), .enable("false")) multiplexer_17 (
    .in0(bit_extender_4_out), .in1(main_1_reg2_2), .out(multiplexer_17_out), .sel(and_9_out));
  and and_9 (and_9_out, demultiplexer_2_out3, mtc0);
  Button ISRC0_2 (.out(ISRC0_2_out));
  Button ISRC1_2 (.out(ISRC1_2_out));
  Button ISRC2_2 (.out(ISRC2_2_out));
  Multiplexer #(.width(32), .enable("false")) multiplexer_18 (
    .in0({ram_1_data_2, main_1_reg2_2[15:0]}), .in1({main_1_reg2_2[15:0], ram_1_data}),
    .out(multiplexer_18_out), .sel(highlow));
  Multiplexer #(.width(32), .enable("false")) multiplexer_19 (
    .in0(main_1_reg2_2), .in1(pcbuf), .out(multiplexer_19_out), .sel(IS0));
  or or_4 (or_4_out, and_7_out, IS0);
  or or_5 (or_5_out, IS0, and_9_out);
  Register #(.width(1)) IR0 (.D(1'b1), .en(1'b1), .Q(I0), .clk(ISRC0_2_out), .clr(demultiplexer_3_out1));
  Register #(.width(1)) IR1 (.D(1'b1), .en(1'b1), .Q(I1), .clk(ISRC1_2_out), .clr(demultiplexer_3_out2));
  Register #(.width(1)) IR2 (.D(1'b1), .en(1'b1), .Q(I2), .clk(ISRC2_2_out), .clr(demultiplexer_3_out3));
  Multiplexer #(.width(32), .enable("false")) multiplexer_20 (
    .in0(main_1_reg2_2), .in1(multiplexer_18_out), .out(multiplexer_20_out), .sel(sh));
  Register #(.width(32)) u_EPC (.D(multiplexer_19_out), .en(or_4_out), .Q(epc), .clk(clk), .clr(1'b0));
  Register #(.width(32)) STATUS (.D(main_1_reg2_2), .en(and_8_out), .Q({STATUS_q, IE}), .clk(clk), .clr(1'b0));
  Register #(.width(32)) CAUSE (.D(multiplexer_17_out), .en(or_5_out), .Q(CAUSE_q), .clk(clk), .clr(1'b0));
  Demultiplexer #(.select(2), .enable("false")) demultiplexer_3 (
    .out1(demultiplexer_3_out1), .out2(demultiplexer_3_out2), .out3(demultiplexer_3_out3), .in(and_15_out),
    .sel(CAUSE_q[1:0]));  // open: out0
  RAM #(.addrWidth(24), .dataWidth(32), .bus("separate")) ram_1 (
    .addr(alu_1_p5[25:2]), .din(multiplexer_20_out), .data({ram_1_data_2, ram_1_data}), .str(MenWrite),
    .sel(1'b1), .clk(clk), .ld(1'b1), .clr(1'b0));
  Multiplexer #(.select(2), .width(32), .enable("false")) multiplexer_21 (
    .in0({32{1'b0}}), .in1(epc), .in2({STATUS_q, IE}), .in3(CAUSE_q), .out(cp0data), .sel(rd[1:0]));
  Multiplexer #(.width(32), .enable("false")) multiplexer_22 (
    .in0({alu_1_p5, highlow, less}), .in1({ram_1_data_2, ram_1_data}), .out(multiplexer_22_out),
    .sel(MentoReg));
  or or_6 (or_6_out, CAUSE_q[0], CAUSE_q[1]);
  and and_10 (and_10_out, CAUSE_q[0], CAUSE_q[1]);
  assign bit_extender_4_out = {{30{1'b0}}, priority_encoder_1_out};  // Bit_Extender bit_extender_4
  and and_11 (and_11_out, I0, ~or_6_out);  // AND_Gate
  and and_12 (and_12_out, I1, ~CAUSE_q[1]);  // AND_Gate
  and and_13 (and_13_out, I2, ~and_10_out);  // AND_Gate
  Priority_Encoder #(.select(2)) priority_encoder_1 (
    .in0(1'b0), .in1(and_11_out), .in2(and_12_out), .in3(and_13_out), .out(priority_encoder_1_out),
    .gs(priority_encoder_1_gs), .en_out(priority_encoder_1_en_out), .en_in(1'b1));
  and and_14 (IS0, priority_encoder_1_gs, ~IE, ~eret);  // AND_Gate
  D_Flip_Flop d_ff_1 (.clk(clk), .D(IS0), .Q(IS), .preset(1'b0), .en(1'b1), .reset(and_15_out));  // open: Qn
  and and_15 (and_15_out, ~clk, IS);  // AND_Gate
  not not_5 (not_5_out, halt);
  or or_7 (or_7_out, MenWrite, MentoReg);
  Counter #(.width(12), .max('hfff)) counter_1 (
    .D({12{1'b0}}), .count(1'b1), .Q(counter_1_q), .clk(clk), .clr(1'b0));  // open: load, carry
  or or_8 (or_8_out, j, jr);
  or or_9 (or_9_out, beq, bne);
  assign finish = {{11{1'b0}}, not_5_out};  // Bit_Extender bit_extender_5
  Counter #(.width(12), .max('hfff)) counter_2 (
    .load(1'b0), .D({12{1'b0}}), .count(alucount), .Q(counter_2_q), .clk(clk), .clr(1'b0));  // open: carry
  // Probe on counter_2_q
  // Probe on counter_3_q
  Counter #(.width(12), .max('hfff)) counter_3 (
    .load(1'b0), .D({12{1'b0}}), .count(or_7_out), .Q(counter_3_q), .clk(clk), .clr(1'b0));  // open: carry
  Counter #(.width(12), .max('hfff)) counter_4 (
    .load(1'b0), .D({12{1'b0}}), .count(other), .Q(counter_4_q), .clk(clk), .clr(1'b0));  // open: carry
  // Probe on adder_3_out
  Adder #(.width(12)) adder_3 (.a(counter_1_q), .b(finish), .out(adder_3_out), .cin(1'b0));  // open: cout
  // Probe on counter_5_q
  Counter #(.width(12), .max('hfff)) counter_5 (
    .load(1'b0), .D({12{1'b0}}), .count(or_8_out), .Q(counter_5_q), .clk(clk), .clr(1'b0));  // open: carry
  // Probe on counter_6_q
  Counter #(.width(12), .max('hfff)) counter_6 (
    .load(1'b0), .D({12{1'b0}}), .count(or_9_out), .Q(counter_6_q), .clk(clk), .clr(1'b0));  // open: carry
  // Probe on adder_4_out
  Adder #(.width(12)) adder_4 (.a(counter_4_q), .b(finish), .out(adder_4_out), .cin(1'b0));  // open: cout

  // Notes on the sheet:
  //   contents of rom_1 (hex, n*v repeats v):
  //   20110001 8000c05 20110001 20120002 20130003 8000c09 20110001 20120002 20130003 8000c0d 20110001
  //   20120002 20130003 8000c11 20110001 20120002 20130003 c000cb8 20100001 20110001 118fc0 112020
  //   20020022 c 118882 12200001 8000c15 112020 20020022 c 20110001 118880 112020 20020022 c 12200001
  //   8000c1f 20110001 118fc0 112020 20020022 c 1188c3 112020 20020022 c 118903 112020 20020022 c 118903
  //   112020 20020022 c 118903 112020 20020022 c 118903 112020 20020022 c 118903 112020 20020022 c 118903
  //   112020 20020022 c 118903 112020 20020022 c 20100001 109fc0 139fc3 8021 2012000c 24160003 26100001
  //   3210000f 20080008 20090001 139900 2709825 132020 20020022 c 1094022 1500fff9 22100001 2018000f
  //   2188024 108700 20080008 20090001 139902 2709825 132021 20020022 c 1094022 1500fff9 108702 2c9b022
  //   12c00001 8000c50 4020 1084027 84400 3508ffff 82021 20020022 c 2010ffff 20110000 ae300000 22100001
  //   22310004 ae300000 22100001 22310004 ae300000 22100001 22310004 ae300000 22100001 22310004 ae300000
  //   22100001 22310004 ae300000 22100001 22310004 ae300000 22100001 22310004 ae300000 22100001 22310004
  //   ae300000 22100001 22310004 ae300000 22100001 22310004 ae300000 22100001 22310004 ae300000 22100001
  //   22310004 ae300000 22100001 22310004 ae300000 22100001 22310004 ae300000 22100001 22310004 ae300000
  //   22100001 22310004 22100001 8020 2011003c 8e130000 8e340000 274402a 11000002 ae330000 ae140000
  //   2231fffc 1611fff8 102020 20020022 c 22100004 2011003c 1611fff2 2002000a c 20100000 22100001 102020
  //   20020022 c 22100002 102020 20020022 c 22100003 102020 20020022 c 22100004 102020 20020022 c 22100005
  //   102020 20020022 c 22100006 102020 20020022 c 22100007 102020 20020022 c 22100008 102020 20020022
  //   20020022 c 3e00008
  //   contents of rom_2 (hex, n*v repeats v):
  //   201a0001 409a1000 201c0800 39df020 401a0800 afda0000 23defffc 23bdfffc afc40000 23bdfffc 23defffc
  //   afc20000 23bdfffc 23defffc afc80000 23bdfffc 23defffc afc90000 23bdfffc 23defffc afca0000 23bdfffc
  //   23defffc 2009ffe8 13a90004 afc80000 23defffc 23bdfffc 15200004 20090000 afc90000 23defffc 23bdfffc
  //   201a0000 409a1000 40081800 20020003 11020008 20090008 82020 200a0001 c 42100 12a4822 1520fffc
  //   11200010 20044000 20090001 200a0804 c 214a0002 1242007 a5440001 1c80fffb 20040aaa 20090555 892026 c
  //   20040aaa 20090aaa 892026 c 201a0001 409a1000 23de0004 23bd0004 8fda0000 409a1800 23de0004 23bd0004
  //   8fca0000 23de0004 23bd0004 8fc90000 23de0004 23bd0004 8fc80000 23de0004 23bd0004 8fc20000 23de0004
  //   23bd0004 8fc40000 23de0004 23bd0004 8fda0000 409a0800 201a0000 409a1000 42000018
endmodule

module ControlUnit (
  input  [4:0] Rs,
  input  [5:0] Op,
  input  [5:0] Funct,
  output alucount,
  output other_count,
  output mtc0,
  output mfc0,
  output eret,
  output srav,
  output sh,
  output bgtz,
  output syscall,
  output jal,
  output bne,
  output beq,
  output jr,
  output MentoReg,
  output j,
  output MemWrite,
  output shift,
  output RegDst,
  output RegWrite,
  output ALUSrc,
  output [3:0] ALUControl
);

  wire ADD_out, AND_out, OR_12_out, SLT_out, SUB_out, type1_1_add, type1_1_addi, type1_1_addiu, type1_1_addu,
       type1_1_and, type1_1_andi, type1_1_or, type1_1_ori, type1_1_sll, type1_1_sra, type1_1_srl,
       type1_1_sub, type2_1_j, type2_1_nor, type2_1_slt, type2_1_slti, type2_1_sltu, type2_1_sw, type3_1_xor;

  type0 type0_1 (
    .op0(Op[0]), .op1(Op[1]), .op2(Op[2]), .op3(Op[3]), .op4(Op[4]), .op5(Op[5]), .rs0(Rs[0]), .rs1(Rs[1]),
    .rs2(Rs[2]), .rs3(Rs[3]), .rs4(Rs[4]), .mfc0(mfc0), .mtc0(mtc0));
  type3 type3_1 (
    .op0(Op[0]), .op1(Op[1]), .op2(Op[2]), .op3(Op[3]), .op4(Op[4]), .op5(Op[5]), .funct0(Funct[0]),
    .funct1(Funct[1]), .funct2(Funct[2]), .funct3(Funct[3]), .funct4(Funct[4]), .funct5(Funct[5]),
    .srav(srav), .\xor (type3_1_xor), .sh(sh), .bgtz(bgtz), .eret(eret));
  type1 type1_1 (
    .op0(Op[0]), .op1(Op[1]), .op2(Op[2]), .op3(Op[3]), .op4(Op[4]), .op5(Op[5]), .funct0(Funct[0]),
    .funct1(Funct[1]), .funct2(Funct[2]), .funct3(Funct[3]), .funct4(Funct[4]), .funct5(Funct[5]),
    .add(type1_1_add), .addi(type1_1_addi), .addiu(type1_1_addiu), .addu(type1_1_addu), .\and (type1_1_and),
    .andi(type1_1_andi), .sll(type1_1_sll), .sra(type1_1_sra), .srl(type1_1_srl), .sub(type1_1_sub),
    .\or (type1_1_or), .ori(type1_1_ori));
  type2 type2_1 (
    .op0(Op[0]), .op1(Op[1]), .op2(Op[2]), .op3(Op[3]), .op4(Op[4]), .op5(Op[5]), .funct0(Funct[0]),
    .funct1(Funct[1]), .funct2(Funct[2]), .funct3(Funct[3]), .funct4(Funct[4]), .funct5(Funct[5]),
    .\nor (type2_1_nor), .lw(MentoReg), .sw(type2_1_sw), .beq(beq), .bne(bne), .slt(type2_1_slt),
    .slti(type2_1_slti), .sltu(type2_1_sltu), .j(type2_1_j), .jal(jal), .jr(jr), .syscall(syscall));
  or or_1 (other_count, syscall, type2_1_sltu, type2_1_slti, type2_1_slt, type1_1_addu);
  or or_2 (alucount, type1_1_add, type1_1_addi, type1_1_addiu, type1_1_and, type1_1_andi, type1_1_sll, type1_1_sra, type1_1_srl, type1_1_sub, type1_1_or, type1_1_ori, type2_1_nor);
  or or_3 (j, jal, type2_1_j);
  or or_4 (MemWrite, type2_1_sw, sh);
  or or_5 (shift, type1_1_srl, type1_1_sra, type1_1_sll);
  or or_6 (RegDst, srav, type2_1_sltu, type2_1_slt, type2_1_nor, type1_1_or, type1_1_sub, type1_1_srl, type1_1_sra, type1_1_sll, type1_1_and, type1_1_addu, type1_1_add, type3_1_xor);
  or or_7 (RegWrite, srav, jal, type2_1_sltu, type2_1_slti, type2_1_slt, MentoReg, type2_1_nor, type1_1_ori, type1_1_or, type1_1_sub, mfc0, type1_1_srl, type1_1_sra, type1_1_sll, type1_1_andi, type1_1_and, type1_1_addu, type1_1_addiu, type1_1_addi, type1_1_add, type3_1_xor);
  or or_8 (ALUSrc, sh, type2_1_slti, type2_1_sw, MentoReg, type1_1_ori, type1_1_andi, type1_1_addiu, type1_1_addi);
  or ADD (ADD_out, type2_1_sw, MentoReg, type1_1_addu, type1_1_addiu, type1_1_addi, type1_1_add);
  or or_9 (ALUControl[3], type3_1_xor, type2_1_sltu, type2_1_nor, OR_12_out, SLT_out, bgtz);
  or SUB (SUB_out, bne, beq, type1_1_sub);
  or or_10 (ALUControl[2], type2_1_sltu, ADD_out, sh, SUB_out, AND_out);
  or AND (AND_out, type1_1_andi, type1_1_and);
  or or_11 (ALUControl[1], AND_out, type1_1_srl, type2_1_nor, SUB_out, SLT_out, bgtz);
  or OR_12 (OR_12_out, type1_1_ori, type1_1_or);
  or SLT (SLT_out, type2_1_slti, type2_1_slt);
  or or_13 (ALUControl[0], bgtz, type3_1_xor, type1_1_sra, ADD_out, AND_out, SLT_out, srav, sh);
endmodule

module DI (
  input  [31:0] IR,
  output [25:0] imm_26bit,
  output [15:0] imm_16bit,
  output [5:0] funct,
  output [4:0] sa,
  output [4:0] rd,
  output [4:0] rt,
  output [4:0] rs,
  output [5:0] op
);


  assign funct = IR[5:0];
  assign imm_16bit = IR[15:0];
  assign imm_26bit = IR[25:0];
  assign op = IR[31:26];
  assign rd = IR[15:11];
  assign rs = IR[25:21];
  assign rt = IR[20:16];
  assign sa = IR[10:6];
endmodule

module type1 (
  input  op0,
  input  op1,
  input  op2,
  input  op3,
  input  op4,
  input  op5,
  input  funct0,
  input  funct1,
  input  funct2,
  input  funct3,
  input  funct4,
  input  funct5,
  output add,
  output addi,
  output addiu,
  output addu,
  output \and ,
  output andi,
  output sll,
  output sra,
  output srl,
  output sub,
  output \or ,
  output ori
);

  wire not_1_out, not_2_out, not_3_out, not_4_out, not_5_out, not_6_out, not_7_out, not_8_out, not_9_out,
       not_10_out, not_11_out, not_12_out, not_13_out, not_14_out, not_15_out, not_16_out, not_17_out,
       not_18_out, not_19_out, not_20_out, not_21_out, not_22_out, not_23_out, not_24_out, not_25_out,
       not_26_out, not_27_out, not_28_out, not_29_out, not_30_out, not_31_out, not_32_out, not_33_out,
       not_34_out, not_35_out, not_36_out, not_37_out, not_38_out, not_39_out, not_40_out, not_41_out,
       not_42_out, not_43_out, not_44_out, not_45_out, not_46_out, not_47_out, not_48_out, not_49_out,
       not_50_out, not_51_out, not_52_out, not_53_out, not_54_out, not_55_out, not_56_out, not_57_out,
       not_58_out, not_59_out, not_60_out, not_61_out, not_62_out, not_63_out, not_64_out, not_65_out,
       not_66_out, not_67_out, not_68_out, not_69_out, not_70_out, not_71_out, not_72_out, not_73_out,
       not_74_out, not_75_out, not_76_out, not_77_out, not_78_out, not_79_out, not_80_out, not_81_out,
       not_82_out, not_83_out, not_84_out, not_85_out, not_86_out, not_87_out, not_88_out, not_89_out,
       not_90_out, not_91_out, not_92_out, not_93_out, not_94_out, not_95_out, not_96_out, not_97_out,
       not_98_out, not_99_out;

  not not_1 (not_1_out, op5);
  not not_2 (not_2_out, op4);
  not not_3 (not_3_out, op3);
  not not_4 (not_4_out, op2);
  not not_5 (not_5_out, op1);
  not not_6 (not_6_out, op0);
  not not_7 (not_7_out, funct4);
  not not_8 (not_8_out, funct3);
  not not_9 (not_9_out, funct2);
  not not_10 (not_10_out, funct1);
  not not_11 (not_11_out, funct0);
  not not_12 (not_12_out, op5);
  not not_13 (not_13_out, op4);
  not not_14 (not_14_out, op2);
  not not_15 (not_15_out, op1);
  not not_16 (not_16_out, op0);
  not not_17 (not_17_out, op5);
  not not_18 (not_18_out, op4);
  not not_19 (not_19_out, op2);
  not not_20 (not_20_out, op1);
  not not_21 (not_21_out, op5);
  not not_22 (not_22_out, op4);
  not not_23 (not_23_out, op3);
  not not_24 (not_24_out, op2);
  not not_25 (not_25_out, op1);
  not not_26 (not_26_out, op0);
  not not_27 (not_27_out, funct4);
  not not_28 (not_28_out, funct3);
  not not_29 (not_29_out, funct2);
  not not_30 (not_30_out, funct1);
  not not_31 (not_31_out, op5);
  not not_32 (not_32_out, op4);
  not not_33 (not_33_out, op3);
  not not_34 (not_34_out, op2);
  not not_35 (not_35_out, op1);
  not not_36 (not_36_out, op0);
  not not_37 (not_37_out, funct4);
  not not_38 (not_38_out, funct3);
  not not_39 (not_39_out, funct1);
  not not_40 (not_40_out, funct0);
  not not_41 (not_41_out, op5);
  not not_42 (not_42_out, op4);
  not not_43 (not_43_out, op1);
  not not_44 (not_44_out, op0);
  not not_45 (not_45_out, op5);
  not not_46 (not_46_out, op4);
  not not_47 (not_47_out, op3);
  not not_48 (not_48_out, op2);
  not not_49 (not_49_out, op1);
  not not_50 (not_50_out, op0);
  not not_51 (not_51_out, funct5);
  not not_52 (not_52_out, funct4);
  not not_53 (not_53_out, funct3);
  not not_54 (not_54_out, funct2);
  not not_55 (not_55_out, funct1);
  not not_56 (not_56_out, funct0);
  not not_57 (not_57_out, op5);
  not not_58 (not_58_out, op4);
  not not_59 (not_59_out, op3);
  not not_60 (not_60_out, op2);
  not not_61 (not_61_out, op1);
  not not_62 (not_62_out, op0);
  not not_63 (not_63_out, funct5);
  not not_64 (not_64_out, funct4);
  not not_65 (not_65_out, funct3);
  not not_66 (not_66_out, funct2);
  not not_67 (not_67_out, op5);
  not not_68 (not_68_out, op4);
  not not_69 (not_69_out, op3);
  not not_70 (not_70_out, op2);
  not not_71 (not_71_out, op1);
  not not_72 (not_72_out, op0);
  not not_73 (not_73_out, funct5);
  not not_74 (not_74_out, funct4);
  not not_75 (not_75_out, funct3);
  not not_76 (not_76_out, funct2);
  not not_77 (not_77_out, funct0);
  not not_78 (not_78_out, op5);
  not not_79 (not_79_out, op4);
  not not_80 (not_80_out, op3);
  not not_81 (not_81_out, op2);
  not not_82 (not_82_out, op1);
  not not_83 (not_83_out, op0);
  not not_84 (not_84_out, funct4);
  not not_85 (not_85_out, funct3);
  not not_86 (not_86_out, funct2);
  not not_87 (not_87_out, funct0);
  not not_88 (not_88_out, op5);
  not not_89 (not_89_out, op4);
  not not_90 (not_90_out, op3);
  not not_91 (not_91_out, op2);
  not not_92 (not_92_out, op1);
  not not_93 (not_93_out, op0);
  not not_94 (not_94_out, funct4);
  not not_95 (not_95_out, funct3);
  not not_96 (not_96_out, funct1);
  not not_97 (not_97_out, op5);
  not not_98 (not_98_out, op4);
  not not_99 (not_99_out, op1);
  and and_1 (add, not_1_out, not_2_out, not_3_out, not_4_out, not_5_out, not_6_out, funct5, not_7_out, not_8_out, not_9_out, not_10_out, not_11_out);
  and and_2 (addi, not_12_out, not_13_out, op3, not_14_out, not_15_out, not_16_out);
  and and_3 (addiu, not_17_out, not_18_out, op3, not_19_out, not_20_out, op0);
  and and_4 (addu, not_21_out, not_22_out, not_23_out, not_24_out, not_25_out, not_26_out, funct5, not_27_out, not_28_out, not_29_out, not_30_out, funct0);
  and and_5 (\and , not_31_out, not_32_out, not_33_out, not_34_out, not_35_out, not_36_out, funct5, not_37_out, not_38_out, funct2, not_39_out, not_40_out);
  and and_6 (andi, not_41_out, not_42_out, op3, op2, not_43_out, not_44_out);
  and and_7 (sll, not_45_out, not_46_out, not_47_out, not_48_out, not_49_out, not_50_out, not_51_out, not_52_out, not_53_out, not_54_out, not_55_out, not_56_out);
  and and_8 (sra, not_57_out, not_58_out, not_59_out, not_60_out, not_61_out, not_62_out, not_63_out, not_64_out, not_65_out, not_66_out, funct1, funct0);
  and and_9 (srl, not_67_out, not_68_out, not_69_out, not_70_out, not_71_out, not_72_out, not_73_out, not_74_out, not_75_out, not_76_out, funct1, not_77_out);
  and and_10 (sub, not_78_out, not_79_out, not_80_out, not_81_out, not_82_out, not_83_out, funct5, not_84_out, not_85_out, not_86_out, funct1, not_87_out);
  and and_11 (\or , not_88_out, not_89_out, not_90_out, not_91_out, not_92_out, not_93_out, funct5, not_94_out, not_95_out, funct2, not_96_out, funct0);
  and and_12 (ori, not_97_out, not_98_out, op3, op2, not_99_out, op0);
endmodule

module type2 (
  input  op0,
  input  op1,
  input  op2,
  input  op3,
  input  op4,
  input  op5,
  input  funct0,
  input  funct1,
  input  funct2,
  input  funct3,
  input  funct4,
  input  funct5,
  output \nor ,
  output lw,
  output sw,
  output beq,
  output bne,
  output slt,
  output slti,
  output sltu,
  output j,
  output jal,
  output jr,
  output syscall
);

  wire not_1_out, not_2_out, not_3_out, not_4_out, not_5_out, not_6_out, not_7_out, not_8_out, not_9_out,
       not_10_out, not_11_out, not_12_out, not_13_out, not_14_out, not_15_out, not_16_out, not_17_out,
       not_18_out, not_19_out, not_20_out, not_21_out, not_22_out, not_23_out, not_24_out, not_25_out,
       not_26_out, not_27_out, not_28_out, not_29_out, not_30_out, not_31_out, not_32_out, not_33_out,
       not_34_out, not_35_out, not_36_out, not_37_out, not_38_out, not_39_out, not_40_out, not_41_out,
       not_42_out, not_43_out, not_44_out, not_45_out, not_46_out, not_47_out, not_48_out, not_49_out,
       not_50_out, not_51_out, not_52_out, not_53_out, not_54_out, not_55_out, not_56_out, not_57_out,
       not_58_out, not_59_out, not_60_out, not_61_out, not_62_out, not_63_out, not_64_out, not_65_out,
       not_66_out, not_67_out, not_68_out, not_69_out, not_70_out, not_71_out, not_72_out, not_73_out;

  not not_1 (not_1_out, op5);
  not not_2 (not_2_out, op4);
  not not_3 (not_3_out, op3);
  not not_4 (not_4_out, op2);
  not not_5 (not_5_out, op1);
  not not_6 (not_6_out, op0);
  not not_7 (not_7_out, funct4);
  not not_8 (not_8_out, funct3);
  not not_9 (not_9_out, op4);
  not not_10 (not_10_out, op3);
  not not_11 (not_11_out, op2);
  not not_12 (not_12_out, op4);
  not not_13 (not_13_out, op2);
  not not_14 (not_14_out, op5);
  not not_15 (not_15_out, op4);
  not not_16 (not_16_out, op3);
  not not_17 (not_17_out, op1);
  not not_18 (not_18_out, op0);
  not not_19 (not_19_out, op5);
  not not_20 (not_20_out, op4);
  not not_21 (not_21_out, op3);
  not not_22 (not_22_out, op1);
  not not_23 (not_23_out, op5);
  not not_24 (not_24_out, op4);
  not not_25 (not_25_out, op3);
  not not_26 (not_26_out, op2);
  not not_27 (not_27_out, op1);
  not not_28 (not_28_out, op0);
  not not_29 (not_29_out, funct4);
  not not_30 (not_30_out, funct2);
  not not_31 (not_31_out, funct0);
  not not_32 (not_32_out, op5);
  not not_33 (not_33_out, op4);
  not not_34 (not_34_out, op2);
  not not_35 (not_35_out, op0);
  not not_36 (not_36_out, op5);
  not not_37 (not_37_out, op4);
  not not_38 (not_38_out, op3);
  not not_39 (not_39_out, op2);
  not not_40 (not_40_out, op1);
  not not_41 (not_41_out, op0);
  not not_42 (not_42_out, funct4);
  not not_43 (not_43_out, funct2);
  not not_44 (not_44_out, op5);
  not not_45 (not_45_out, op4);
  not not_46 (not_46_out, op3);
  not not_47 (not_47_out, op2);
  not not_48 (not_48_out, op0);
  not not_49 (not_49_out, op5);
  not not_50 (not_50_out, op4);
  not not_51 (not_51_out, op3);
  not not_52 (not_52_out, op2);
  not not_53 (not_53_out, op5);
  not not_54 (not_54_out, op4);
  not not_55 (not_55_out, op3);
  not not_56 (not_56_out, op2);
  not not_57 (not_57_out, op1);
  not not_58 (not_58_out, op0);
  not not_59 (not_59_out, funct5);
  not not_60 (not_60_out, funct4);
  not not_61 (not_61_out, funct2);
  not not_62 (not_62_out, funct1);
  not not_63 (not_63_out, funct0);
  not not_64 (not_64_out, op5);
  not not_65 (not_65_out, op4);
  not not_66 (not_66_out, op3);
  not not_67 (not_67_out, op2);
  not not_68 (not_68_out, op1);
  not not_69 (not_69_out, op0);
  not not_70 (not_70_out, funct5);
  not not_71 (not_71_out, funct4);
  not not_72 (not_72_out, funct1);
  not not_73 (not_73_out, funct0);
  and and_1 (\nor , not_1_out, not_2_out, not_3_out, not_4_out, not_5_out, not_6_out, funct5, not_7_out, not_8_out, funct2, funct1, funct0);
  and and_2 (lw, op5, not_9_out, not_10_out, not_11_out, op1, op0);
  and and_3 (sw, op5, not_12_out, op3, not_13_out, op1, op0);
  and and_4 (beq, not_14_out, not_15_out, not_16_out, op2, not_17_out, not_18_out);
  and and_5 (bne, not_19_out, not_20_out, not_21_out, op2, not_22_out, op0);
  and and_6 (slt, not_23_out, not_24_out, not_25_out, not_26_out, not_27_out, not_28_out, funct5, not_29_out, funct3, not_30_out, funct1, not_31_out);
  and and_7 (slti, not_32_out, not_33_out, op3, not_34_out, op1, not_35_out);
  and and_8 (sltu, not_36_out, not_37_out, not_38_out, not_39_out, not_40_out, not_41_out, funct5, not_42_out, funct3, not_43_out, funct1, funct0);
  and and_9 (j, not_44_out, not_45_out, not_46_out, not_47_out, op1, not_48_out);
  and and_10 (jal, not_49_out, not_50_out, not_51_out, not_52_out, op1, op0);
  and and_11 (jr, not_53_out, not_54_out, not_55_out, not_56_out, not_57_out, not_58_out, not_59_out, not_60_out, funct3, not_61_out, not_62_out, not_63_out);
  and and_12 (syscall, not_64_out, not_65_out, not_66_out, not_67_out, not_68_out, not_69_out, not_70_out, not_71_out, funct3, funct2, not_72_out, not_73_out);
endmodule

module type3 (
  input  op0,
  input  op1,
  input  op2,
  input  op3,
  input  op4,
  input  op5,
  input  funct0,
  input  funct1,
  input  funct2,
  input  funct3,
  input  funct4,
  input  funct5,
  output srav,
  output \xor ,
  output sh,
  output bgtz,
  output eret
);

  wire not_1_out, not_2_out, not_3_out, not_4_out, not_5_out, not_6_out, not_7_out, not_8_out, not_9_out,
       not_10_out, not_11_out, not_12_out, not_13_out, not_14_out, not_15_out, not_16_out, not_17_out,
       not_18_out, not_19_out, not_20_out, not_21_out, not_22_out, not_23_out, not_24_out, not_25_out,
       not_26_out, not_27_out, not_28_out, not_29_out, not_30_out, not_31_out, not_32_out, not_33_out;

  not not_1 (not_1_out, op5);
  not not_2 (not_2_out, op4);
  not not_3 (not_3_out, op3);
  not not_4 (not_4_out, op2);
  not not_5 (not_5_out, op1);
  not not_6 (not_6_out, op0);
  not not_7 (not_7_out, funct5);
  not not_8 (not_8_out, funct4);
  not not_9 (not_9_out, funct3);
  not not_10 (not_10_out, op5);
  not not_11 (not_11_out, op4);
  not not_12 (not_12_out, op3);
  not not_13 (not_13_out, op2);
  not not_14 (not_14_out, op1);
  not not_15 (not_15_out, op0);
  not not_16 (not_16_out, funct4);
  not not_17 (not_17_out, funct3);
  not not_18 (not_18_out, funct0);
  not not_19 (not_19_out, op4);
  not not_20 (not_20_out, op2);
  not not_21 (not_21_out, op1);
  not not_22 (not_22_out, op5);
  not not_23 (not_23_out, op4);
  not not_24 (not_24_out, op3);
  not not_25 (not_25_out, op5);
  not not_26 (not_26_out, op3);
  not not_27 (not_27_out, op2);
  not not_28 (not_28_out, op1);
  not not_29 (not_29_out, op0);
  not not_30 (not_30_out, funct5);
  not not_31 (not_31_out, funct2);
  not not_32 (not_32_out, funct1);
  not not_33 (not_33_out, funct0);
  and and_1 (srav, not_1_out, not_2_out, not_3_out, not_4_out, not_5_out, not_6_out, not_7_out, not_8_out, not_9_out, funct2, funct1, funct0);
  and and_2 (\xor , not_10_out, not_11_out, not_12_out, not_13_out, not_14_out, not_15_out, funct5, not_16_out, not_17_out, funct2, funct1, not_18_out);
  and and_3 (sh, op5, not_19_out, op3, not_20_out, not_21_out, op0);
  and and_4 (bgtz, not_22_out, not_23_out, not_24_out, op2, op1, op0);
  and and_5 (eret, not_25_out, op4, not_26_out, not_27_out, not_28_out, not_29_out, not_30_out, funct4, funct3, not_31_out, not_32_out, not_33_out);
endmodule

module type0 (
  input  op0,
  input  op1,
  input  op2,
  input  op3,
  input  op4,
  input  op5,
  input  rs0,
  input  rs1,
  input  rs2,
  input  rs3,
  input  rs4,
  output mfc0,
  output mtc0
);

  wire not_1_out, not_2_out, not_3_out, not_4_out, not_5_out, not_6_out, not_7_out, not_8_out, not_9_out,
       not_10_out, not_11_out, not_12_out, not_13_out, not_14_out, not_15_out, not_16_out, not_17_out,
       not_18_out, not_19_out;

  not not_1 (not_1_out, op5);
  not not_2 (not_2_out, op3);
  not not_3 (not_3_out, op2);
  not not_4 (not_4_out, op1);
  not not_5 (not_5_out, op0);
  not not_6 (not_6_out, rs4);
  not not_7 (not_7_out, rs3);
  not not_8 (not_8_out, rs2);
  not not_9 (not_9_out, rs1);
  not not_10 (not_10_out, rs0);
  not not_11 (not_11_out, op5);
  not not_12 (not_12_out, op3);
  not not_13 (not_13_out, op2);
  not not_14 (not_14_out, op1);
  not not_15 (not_15_out, op0);
  not not_16 (not_16_out, rs4);
  not not_17 (not_17_out, rs3);
  not not_18 (not_18_out, rs1);
  not not_19 (not_19_out, rs0);
  and and_1 (mfc0, not_1_out, op4, not_2_out, not_3_out, not_4_out, not_5_out, not_6_out, not_7_out, not_8_out, not_9_out, not_10_out);
  and and_2 (mtc0, not_11_out, op4, not_12_out, not_13_out, not_14_out, not_15_out, not_16_out, not_17_out, rs2, not_18_out, not_19_out);
endmodule
